// Logisim project pk16.circ as structural Verilog: 59 circuits, main circuit version_2
module main (
);

  wire clock_1_out, mode_1_controller_1_disable_jump, mode_1_controller_1_disable_lower,
       mode_1_controller_1_disable_upper, mode_2_controller_1_disable_lower,
       mode_2_controller_1_disable_upper, mode_3_controller_1_disable_lower,
       mode_3_controller_1_disable_upper, n7400_1_pin1, n7400_1_pin3, n7400_1_pin6, n7400_1_pin8,
       n7400_1_pin13, n7400_2_pin3, n7400_2_pin6, n7400_2_pin8, n7400_2_pin11, n7421_1_pin1, n7421_1_pin6,
       n7421_1_pin8, n74163_1_pin7, n74163_1_pin11, n74163_1_pin13, n74163_1_pin14, not_1_out, not_2_out,
       opcode_decoder_1_not_read_program;
  wire [3:0] bus_encoder_1_p2;
  wire [7:0] bus_encoder_1_p3, bus_encoder_1_p4, bus_encoder_1_p5, bus_encoder_1_p6, rom_chip_1_io, undriven;
  wire [14:0] pull_resistor_1_node;
  wire [15:0] immediate_controller_1_value_2, main_register_1_read_1, main_register_1_read_2,
       main_register_1_value, main_register_2_value, main_register_3_value, main_register_4_value,
       main_register_5_value, main_register_6_value, mode_1_controller_1_jump_addr,
       mode_3_controller_1_write_value, opcode_decoder_1_instruction, program_counter_1_accum,
       register_value_controller_1_value_1;
  wire [15:15] pull_resistor_1_node_2;

  Clock clock_1 (.out(clock_1_out));
  not not_1 (not_1_out, pull_resistor_1_node_2[15]);
  not not_2 (not_2_out, opcode_decoder_1_not_read_program);
  Pull_Resistor pull_resistor_1 (.node({pull_resistor_1_node_2[15], pull_resistor_1_node}));
  program_counter program_counter_1 (
    .count_enable(opcode_decoder_1_not_read_program), .jump_addr(mode_1_controller_1_jump_addr),
    .clock(n7400_1_pin8), .disable_jump(mode_1_controller_1_disable_jump), .accum(program_counter_1_accum));
  tri_state_switch_16 tri_state_switch_16_1 (
    .a(program_counter_1_accum), .disable_output(not_2_out),
    .out_3({pull_resistor_1_node_2[15], pull_resistor_1_node}));
  // Probe on rom_chip_1_io
  rom_chip rom_chip_1 (
    .address(pull_resistor_1_node), .chip_disable(pull_resistor_1_node_2[15]),
    .output_disable(pull_resistor_1_node_2[15]), .write_disable(1'b1), .io(rom_chip_1_io));
  Pull_Resistor pull_resistor_2 (.node(rom_chip_1_io));
  ram_chip ram_chip_1 (
    .address(pull_resistor_1_node), .write_disable(1'b1), .write_value(undriven), .output_disable(not_1_out),
    .read_value(rom_chip_1_io));
  _7400 u_7400_1 (
    .pin1(n7400_1_pin1), .pin2(clock_1_out), .pin3(n7400_1_pin3), .pin4(n7400_1_pin3), .pin5(n7400_1_pin3),
    .pin6(n7400_1_pin6), .pin13(n7400_1_pin13), .pin12(n7400_1_pin13), .pin11(n7400_1_pin1),
    .pin10(clock_1_out), .pin9(clock_1_out), .pin8(n7400_1_pin8));
  _74163 u_74163_1 (
    .pin1(n7400_1_pin1), .pin2(clock_1_out), .pin7(n74163_1_pin7), .pin14(n74163_1_pin14),
    .pin13(n74163_1_pin13), .pin12(n7400_1_pin13), .pin11(n74163_1_pin11), .pin10(n74163_1_pin7),
    .pin9(n74163_1_pin7));  // open: pin3, pin4, pin5, pin6, pin15
  Pull_Resistor #(.pull(1)) pull_resistor_3 (.node(n74163_1_pin7));
  opcode_decoder opcode_decoder_1 (
    .read_inst(rom_chip_1_io), .inst_complete(n7400_1_pin13), .clock(n7400_1_pin6),
    .instruction(opcode_decoder_1_instruction), .not_read_program(opcode_decoder_1_not_read_program));
  immediate_controller immediate_controller_1 (
    .opcode_format(bus_encoder_1_p2), .opcode_lower(bus_encoder_1_p5),
    .value_2(immediate_controller_1_value_2));
  register_value_controller register_value_controller_1 (
    .opcode_format(bus_encoder_1_p2), .register_value_1(main_register_1_read_1),
    .register_value_2(main_register_1_read_2), .value_1(register_value_controller_1_value_1),
    .value_2(immediate_controller_1_value_2));
  // Probe on opcode_decoder_1_instruction
  mode_3_controller mode_3_controller_1 (
    .opcode_format(bus_encoder_1_p2), .opcode_upper(bus_encoder_1_p6),
    .value_2(immediate_controller_1_value_2), .write_value(mode_3_controller_1_write_value),
    .disable_lower(mode_3_controller_1_disable_lower), .disable_upper(mode_3_controller_1_disable_upper));
  mode_2_controller mode_2_controller_1 (
    .opcode_format(bus_encoder_1_p2), .value_1(register_value_controller_1_value_1),
    .value_2(immediate_controller_1_value_2), .opcode_lower(bus_encoder_1_p5),
    .write_value(mode_3_controller_1_write_value), .disable_lower(mode_2_controller_1_disable_lower),
    .disable_upper(mode_2_controller_1_disable_upper));
  mode_1_controller mode_1_controller_1 (
    .opcode_format(bus_encoder_1_p2), .value_1(register_value_controller_1_value_1),
    .value_2(immediate_controller_1_value_2), .opcode_lower(bus_encoder_1_p5),
    .write_value(mode_3_controller_1_write_value), .disable_lower(mode_1_controller_1_disable_lower),
    .disable_upper(mode_1_controller_1_disable_upper), .jump_addr(mode_1_controller_1_jump_addr),
    .disable_jump(mode_1_controller_1_disable_jump));
  // bus_encoder bus_encoder_1: pin names not known; wires that end beside it: opcode_decoder_1_instruction, bus_encoder_1_p2, bus_encoder_1_p3, bus_encoder_1_p4, bus_encoder_1_p5, bus_encoder_1_p6, n7400_1_pin13, bus_encoder_1_p6, bus_encoder_1_p2
  _7421 u_7421_1 (
    .pin1(n7421_1_pin1), .pin2(mode_1_controller_1_disable_upper), .pin4(mode_2_controller_1_disable_upper),
    .pin5(mode_3_controller_1_disable_upper), .pin6(n7421_1_pin6), .pin13(n7421_1_pin1),
    .pin12(mode_1_controller_1_disable_lower), .pin10(mode_2_controller_1_disable_lower),
    .pin9(mode_3_controller_1_disable_lower), .pin8(n7421_1_pin8));  // open: pin3, pin11
  _7400 u_7400_2 (
    .pin1(n7421_1_pin8), .pin2(n7421_1_pin8), .pin3(n7400_2_pin3), .pin4(n7400_2_pin3), .pin5(n7400_1_pin13),
    .pin6(n7400_2_pin6), .pin13(n7421_1_pin6), .pin12(n7421_1_pin6), .pin11(n7400_2_pin11),
    .pin10(n7400_2_pin11), .pin9(n7400_1_pin13), .pin8(n7400_2_pin8));
  main_register main_register_1 (
    .clock(clock_1_out), .not_select_1(bus_encoder_1_p3[0]), .not_select_2(bus_encoder_1_p4[0]),
    .write_value(mode_3_controller_1_write_value), .disable_upper(n7400_2_pin8),
    .disable_lower(n7400_2_pin6), .read_1(main_register_1_read_1), .read_2(main_register_1_read_2),
    .value(main_register_1_value));
  main_register main_register_2 (
    .clock(clock_1_out), .not_select_1(bus_encoder_1_p3[1]), .not_select_2(bus_encoder_1_p4[1]),
    .write_value(mode_3_controller_1_write_value), .disable_upper(n7400_2_pin8),
    .disable_lower(n7400_2_pin6), .read_1(main_register_1_read_1), .read_2(main_register_1_read_2),
    .value(main_register_2_value));
  main_register main_register_3 (
    .clock(clock_1_out), .not_select_1(bus_encoder_1_p3[2]), .not_select_2(bus_encoder_1_p4[2]),
    .write_value(mode_3_controller_1_write_value), .disable_upper(n7400_2_pin8),
    .disable_lower(n7400_2_pin6), .read_1(main_register_1_read_1), .read_2(main_register_1_read_2),
    .value(main_register_3_value));
  main_register main_register_4 (
    .clock(clock_1_out), .not_select_1(bus_encoder_1_p3[3]), .not_select_2(bus_encoder_1_p4[3]),
    .write_value(mode_3_controller_1_write_value), .disable_upper(n7400_2_pin8),
    .disable_lower(n7400_2_pin6), .read_1(main_register_1_read_1), .read_2(main_register_1_read_2),
    .value(main_register_4_value));
  main_register main_register_5 (
    .clock(clock_1_out), .not_select_1(bus_encoder_1_p3[4]), .not_select_2(bus_encoder_1_p4[4]),
    .write_value(mode_3_controller_1_write_value), .disable_upper(n7400_2_pin8),
    .disable_lower(n7400_2_pin6), .read_1(main_register_1_read_1), .read_2(main_register_1_read_2),
    .value(main_register_5_value));
  main_register main_register_6 (
    .clock(clock_1_out), .not_select_1(bus_encoder_1_p3[5]), .not_select_2(bus_encoder_1_p4[5]),
    .write_value(mode_3_controller_1_write_value), .disable_upper(n7400_2_pin8),
    .disable_lower(n7400_2_pin6), .read_1(main_register_1_read_1), .read_2(main_register_1_read_2),
    .value(main_register_6_value));
  // Probe on main_register_1_value
  // Probe on main_register_2_value
  // Probe on main_register_3_value
  // Probe on main_register_4_value
  // Probe on main_register_5_value
  // Probe on main_register_6_value
  // also tied to VCC on the sheet: n7421_1_pin1
endmodule

module version_2 (
);

  wire bus_encoder_1_compare, bus_encoder_1_compare_set, bus_encoder_1_flip_mem, bus_encoder_1_logical,
       bus_encoder_1_memory, bus_encoder_1_simple, bus_encoder_1_stack, bus_encoder_1_write_lower,
       bus_encoder_1_write_mem, bus_encoder_1_write_upper, button_1_out, clock_1_out,
       controlled_buffer_1_out, logical_controller_1_not_carry_out, logical_controller_1_not_carry_used,
       memory_controller_1_carry_out, memory_controller_1_not_shutdown, memory_controller_1_ps2a_rec,
       memory_controller_1_ps2b_rec, memory_controller_1_timera_ovf, memory_controller_1_timerb_ovf,
       n7400_1_pin1, n7400_1_pin3, n7400_1_pin6, n7400_1_pin10, n7400_1_pin11, n7400_1_pin13, n7400_2_pin2,
       n7400_2_pin3, n7400_2_pin6, n7400_2_pin8, n7432_1_pin5, n7432_1_pin6, n74125_1_pin2, n74125_1_pin3,
       n74163_1_pin7, register_controller_1_stack_select_1, register_controller_1_stack_select_2,
       temp_gpu_1_clock_out;
  wire [2:0] bus_encoder_1_destination_select, comparison_controller_1_cma_select, n74163_1_pin14;
  wire [5:0] temp_gpu_1_x_pos, temp_gpu_1_y_pos;
  wire [7:0] bit_decoder_3_1_decoded, bus_encoder_1_destination_register, bus_encoder_1_operation_select,
       bus_encoder_1_source_register, bus_encoder_1_write_value, memory_controller_1_pic_a_config,
       memory_controller_1_pic_b_config, memory_controller_1_pic_c_config;
  wire [14:0] temp_gpu_1_color;
  wire [15:0] bus_encoder_1_value_1, comparison_mux_1_out_10, memory_controller_1_pic_a_address,
       memory_controller_1_pic_b_address, memory_controller_1_pic_c_address, opcode_decoder_1_instruction,
       program_counter_1_accum, register_controller_1_out_22, register_controller_1_out_23,
       register_controller_1_out_24, register_controller_1_out_25, register_controller_1_out_26,
       register_controller_1_out_27, register_controller_1_out_29, stack_controller_1_stack_value,
       tri_state_switch_16_1_out_3, tri_state_switch_16_2_out_3;
  wire [15:8] bus_encoder_1_write_value_2;
  wire [26:0] memory_controller_1_ipba_data;

  Clock clock_1 (.out(clock_1_out));
  assign controlled_buffer_1_out = memory_controller_1_not_shutdown ? clock_1_out : 1'bz;  // Controlled_Buffer controlled_buffer_1
  _7432 u_7432_1 (
    .pin4(bit_decoder_3_1_decoded[5]), .pin5(n7432_1_pin5), .pin6(n7432_1_pin6));  // open: pin1, pin2, pin3, pin13, pin12, pin11, pin10, pin9, pin8
  _7400 u_7400_1 (
    .pin1(n7400_1_pin1), .pin2(controlled_buffer_1_out), .pin3(n7400_1_pin3), .pin4(n7400_1_pin3),
    .pin5(n7400_1_pin3), .pin6(n7400_1_pin6), .pin13(n7400_1_pin13), .pin12(n7400_1_pin13),
    .pin11(n7400_1_pin11), .pin10(n7400_1_pin10), .pin9(n7400_1_pin10), .pin8(n7400_1_pin1));
  _7400 u_7400_2 (
    .pin1(n7432_1_pin6), .pin2(n7400_2_pin2), .pin3(n7400_2_pin3), .pin4(n7400_2_pin3), .pin5(n7400_2_pin3),
    .pin6(n7400_2_pin6), .pin10(n7400_2_pin2), .pin9(n7400_2_pin2), .pin8(n7400_2_pin8));  // open: pin13, pin12, pin11
  _74163 u_74163_1 (
    .pin1(n7400_1_pin1), .pin2(controlled_buffer_1_out), .pin7(n74163_1_pin7), .pin14(n74163_1_pin14[0]),
    .pin13(n74163_1_pin14[1]), .pin12(n74163_1_pin14[2]), .pin11(n7400_1_pin10), .pin10(n74163_1_pin7),
    .pin9(n74163_1_pin7));  // open: pin3, pin4, pin5, pin6, pin15
  tri_state_switch_16 tri_state_switch_16_1 (
    .a(bus_encoder_1_value_1), .disable_output(n7400_2_pin8), .out_3(tri_state_switch_16_1_out_3));
  // Probe on program_counter_1_accum
  // Probe on program_counter_1_accum
  program_counter program_counter_1 (
    .count_enable(n7400_1_pin13), .jump_addr(tri_state_switch_16_1_out_3), .clock(controlled_buffer_1_out),
    .disable_jump(n7400_2_pin6), .accum(program_counter_1_accum));
  opcode_decoder opcode_decoder_1 (
    .read_inst(bus_encoder_1_write_value), .inst_complete(n7400_1_pin10), .clock(n7400_1_pin6),
    .instruction(opcode_decoder_1_instruction), .not_read_program(n7400_1_pin13));
  bit_decoder_3 bit_decoder_3_1 (.in_1(n74163_1_pin14), .decoded(bit_decoder_3_1_decoded));
  _74125 u_74125_1 (
    .pin1(n7400_1_pin11), .pin2(n74125_1_pin2), .pin3(n74125_1_pin3));  // open: pin4, pin5, pin6, pin13, pin12, pin11, pin10, pin9, pin8
  // Probe on opcode_decoder_1_instruction
  tri_state_switch_16 tri_state_switch_16_2 (
    .a(program_counter_1_accum), .disable_output(n7400_1_pin11), .out_3(tri_state_switch_16_2_out_3));
  bus_encoder bus_encoder_1 (
    .instruction(opcode_decoder_1_instruction), .execute_disable(n7400_1_pin13),
    .destination_register(bus_encoder_1_destination_register),
    .source_register(bus_encoder_1_source_register), .value_1(bus_encoder_1_value_1),
    .value_2(tri_state_switch_16_2_out_3),
    .write_value({bus_encoder_1_write_value_2, bus_encoder_1_write_value}),
    .instruction_stage(bit_decoder_3_1_decoded[5:3]), .jump(n7432_1_pin5),
    .write_lower(bus_encoder_1_write_lower), .write_upper(bus_encoder_1_write_upper),
    .write_mem(bus_encoder_1_write_mem), .read_mem(n74125_1_pin3), .stack(bus_encoder_1_stack),
    .compare(bus_encoder_1_compare), .logical(bus_encoder_1_logical),
    .compare_set(bus_encoder_1_compare_set), .flip_mem(bus_encoder_1_flip_mem),
    .memory(bus_encoder_1_memory), .simple(bus_encoder_1_simple),
    .operation_select(bus_encoder_1_operation_select), .destination_select(bus_encoder_1_destination_select));
  Pull_Resistor pull_resistor_1 (.node(bus_encoder_1_value_1));
  Pull_Resistor pull_resistor_2 (.node(tri_state_switch_16_2_out_3));
  Pull_Resistor pull_resistor_3 (.node({bus_encoder_1_write_value_2, bus_encoder_1_write_value}));
  Pull_Resistor #(.pull(1)) pull_resistor_4 (.node(n7432_1_pin5));
  Pull_Resistor #(.pull(1)) pull_resistor_5 (.node(bus_encoder_1_write_lower));
  Pull_Resistor #(.pull(1)) pull_resistor_6 (.node(bus_encoder_1_write_upper));
  Pull_Resistor #(.pull(1)) pull_resistor_7 (.node(bus_encoder_1_write_mem));
  Pull_Resistor #(.pull(1)) pull_resistor_8 (.node(n74125_1_pin3));
  Pull_Resistor #(.pull(1)) pull_resistor_9 (.node(bus_encoder_1_stack));
  Pull_Resistor #(.pull(1)) pull_resistor_10 (.node(bus_encoder_1_compare));
  Pull_Resistor #(.pull(1)) pull_resistor_11 (.node(bus_encoder_1_logical));
  Pull_Resistor #(.pull(1)) pull_resistor_12 (.node(bus_encoder_1_compare_set));
  Pull_Resistor #(.pull(1)) pull_resistor_13 (.node(bus_encoder_1_flip_mem));
  Pull_Resistor #(.pull(1)) pull_resistor_14 (.node(bus_encoder_1_memory));
  Pull_Resistor #(.pull(1)) pull_resistor_15 (.node(bus_encoder_1_simple));
  memory_controller memory_controller_1 (
    .not_carry_used(logical_controller_1_not_carry_used), .not_carry_in(logical_controller_1_not_carry_out),
    .value_1(bus_encoder_1_value_1), .value_2(tri_state_switch_16_2_out_3),
    .instruction_stage(bit_decoder_3_1_decoded[5:3]), .jump(n7432_1_pin5),
    .write_lower(bus_encoder_1_write_lower), .write_upper(bus_encoder_1_write_upper),
    .write_mem(bus_encoder_1_write_mem), .read_mem(n74125_1_pin3), .stack(bus_encoder_1_stack),
    .compare(bus_encoder_1_compare), .logical(bus_encoder_1_logical),
    .compare_set(bus_encoder_1_compare_set), .flip_mem(bus_encoder_1_flip_mem),
    .memory(bus_encoder_1_memory), .simple(bus_encoder_1_simple),
    .operation_select(bus_encoder_1_operation_select), .ps2a_rec(memory_controller_1_ps2a_rec),
    .ps2b_rec(memory_controller_1_ps2b_rec), .timera_ovf(memory_controller_1_timera_ovf),
    .timerb_ovf(memory_controller_1_timerb_ovf), .carry_out(memory_controller_1_carry_out),
    .not_shutdown(memory_controller_1_not_shutdown), .pic_a_address(memory_controller_1_pic_a_address),
    .pic_a_config(memory_controller_1_pic_a_config), .pic_b_address(memory_controller_1_pic_b_address),
    .pic_b_config(memory_controller_1_pic_b_config), .pic_c_address(memory_controller_1_pic_c_address),
    .pic_c_config(memory_controller_1_pic_c_config), .ipba_data(memory_controller_1_ipba_data),
    .write_value({bus_encoder_1_write_value_2, bus_encoder_1_write_value}));  // open: ipbb_data
  interrupt_controller interrupt_controller_1 (
    .pic_c_address(memory_controller_1_pic_c_address), .pic_c_config(memory_controller_1_pic_c_config),
    .ps2a(memory_controller_1_ps2a_rec), .ps2b(memory_controller_1_ps2b_rec),
    .timera(memory_controller_1_timera_ovf), .timerb(memory_controller_1_timerb_ovf), .ext(button_1_out),
    .interrupt_stage(bit_decoder_3_1_decoded[6]), .program_counter(program_counter_1_accum),
    .value_1(bus_encoder_1_value_1), .value_2(tri_state_switch_16_2_out_3),
    .instruction_stage(bit_decoder_3_1_decoded[5:3]), .jump(n7432_1_pin5),
    .write_lower(bus_encoder_1_write_lower), .write_upper(bus_encoder_1_write_upper),
    .write_mem(bus_encoder_1_write_mem), .read_mem(n74125_1_pin3), .stack(bus_encoder_1_stack),
    .compare(bus_encoder_1_compare), .logical(bus_encoder_1_logical),
    .compare_set(bus_encoder_1_compare_set), .flip_mem(bus_encoder_1_flip_mem),
    .memory(bus_encoder_1_memory), .simple(bus_encoder_1_simple),
    .operation_select(bus_encoder_1_operation_select), .pic_a_address(memory_controller_1_pic_a_address),
    .pic_a_config(memory_controller_1_pic_a_config), .pic_b_address(memory_controller_1_pic_b_address),
    .pic_b_config(memory_controller_1_pic_b_config), .not_jump(n7400_2_pin2),
    .jump_address(tri_state_switch_16_1_out_3),
    .write_value({bus_encoder_1_write_value_2, bus_encoder_1_write_value}));  // open: b, a
  register_controller register_controller_1 (
    .pc(program_counter_1_accum), .in_1(controlled_buffer_1_out),
    .destination_register(bus_encoder_1_destination_register),
    .source_register(bus_encoder_1_source_register),
    .write_value({bus_encoder_1_write_value_2, bus_encoder_1_write_value}),
    .instruction_stage(bit_decoder_3_1_decoded[5:3]), .jump(n7432_1_pin5),
    .write_lower(bus_encoder_1_write_lower), .write_upper(bus_encoder_1_write_upper),
    .write_mem(bus_encoder_1_write_mem), .read_mem(n74125_1_pin3), .stack(bus_encoder_1_stack),
    .compare(bus_encoder_1_compare), .logical(bus_encoder_1_logical),
    .compare_set(bus_encoder_1_compare_set), .flip_mem(bus_encoder_1_flip_mem),
    .memory(bus_encoder_1_memory), .simple(bus_encoder_1_simple),
    .operation_select(bus_encoder_1_operation_select), .out_29(register_controller_1_out_29),
    .out_26(register_controller_1_out_26), .out_27(register_controller_1_out_27),
    .out_22(register_controller_1_out_22), .out_23(register_controller_1_out_23),
    .out_24(register_controller_1_out_24), .out_25(register_controller_1_out_25),
    .stack_select_1(register_controller_1_stack_select_1),
    .stack_select_2(register_controller_1_stack_select_2), .value_1(bus_encoder_1_value_1),
    .value_2(tri_state_switch_16_2_out_3));
  logical_controller logical_controller_1 (
    .carry_in(memory_controller_1_carry_out), .value_1(bus_encoder_1_value_1),
    .value_2(tri_state_switch_16_2_out_3), .instruction_stage(bit_decoder_3_1_decoded[5:3]),
    .jump(n7432_1_pin5), .write_lower(bus_encoder_1_write_lower), .write_upper(bus_encoder_1_write_upper),
    .write_mem(bus_encoder_1_write_mem), .read_mem(n74125_1_pin3), .stack(bus_encoder_1_stack),
    .compare(bus_encoder_1_compare), .logical(bus_encoder_1_logical),
    .compare_set(bus_encoder_1_compare_set), .flip_mem(bus_encoder_1_flip_mem),
    .memory(bus_encoder_1_memory), .simple(bus_encoder_1_simple),
    .operation_select(bus_encoder_1_operation_select), .not_carry_out(logical_controller_1_not_carry_out),
    .not_carry_used(logical_controller_1_not_carry_used),
    .write_value({bus_encoder_1_write_value_2, bus_encoder_1_write_value}));
  comparison_controller comparison_controller_1 (
    .carry_in(memory_controller_1_carry_out), .destination_select(bus_encoder_1_destination_select),
    .clock(controlled_buffer_1_out), .value_1(bus_encoder_1_value_1), .value_2(tri_state_switch_16_2_out_3),
    .write_value({bus_encoder_1_write_value_2, bus_encoder_1_write_value}),
    .instruction_stage(bit_decoder_3_1_decoded[5:3]), .write_lower(bus_encoder_1_write_lower),
    .write_upper(bus_encoder_1_write_upper), .write_mem(bus_encoder_1_write_mem), .read_mem(n74125_1_pin3),
    .stack(bus_encoder_1_stack), .compare(bus_encoder_1_compare), .logical(bus_encoder_1_logical),
    .compare_set(bus_encoder_1_compare_set), .flip_mem(bus_encoder_1_flip_mem),
    .memory(bus_encoder_1_memory), .simple(bus_encoder_1_simple),
    .operation_select(bus_encoder_1_operation_select), .comp_a(comparison_mux_1_out_10),
    .cma_select(comparison_controller_1_cma_select), .jump(n7432_1_pin5));
  memory_access_controller memory_access_controller_1 (
    .value_1(bus_encoder_1_value_1), .value_2(tri_state_switch_16_2_out_3),
    .instruction_stage(bit_decoder_3_1_decoded[5:3]), .jump(n7432_1_pin5),
    .write_lower(bus_encoder_1_write_lower), .write_upper(bus_encoder_1_write_upper),
    .stack(bus_encoder_1_stack), .compare(bus_encoder_1_compare), .logical(bus_encoder_1_logical),
    .compare_set(bus_encoder_1_compare_set), .memory(bus_encoder_1_memory), .simple(bus_encoder_1_simple),
    .operation_select(bus_encoder_1_operation_select),
    .write_value({bus_encoder_1_write_value_2, bus_encoder_1_write_value}),
    .write_mem(bus_encoder_1_write_mem), .read_mem(n74125_1_pin3), .flip_mem(bus_encoder_1_flip_mem));
  stack_controller stack_controller_1 (
    .stack_select_1(register_controller_1_stack_select_1),
    .stack_select_2(register_controller_1_stack_select_2),
    .write_value({bus_encoder_1_write_value_2, bus_encoder_1_write_value}),
    .instruction_stage(bit_decoder_3_1_decoded[5:3]), .jump(n7432_1_pin5),
    .write_lower(bus_encoder_1_write_lower), .write_upper(bus_encoder_1_write_upper),
    .stack(bus_encoder_1_stack), .compare(bus_encoder_1_compare), .logical(bus_encoder_1_logical),
    .compare_set(bus_encoder_1_compare_set), .memory(bus_encoder_1_memory), .simple(bus_encoder_1_simple),
    .operation_select(bus_encoder_1_operation_select), .stack_value(stack_controller_1_stack_value),
    .value_1(bus_encoder_1_value_1), .value_2(tri_state_switch_16_2_out_3),
    .write_mem(bus_encoder_1_write_mem), .read_mem(n74125_1_pin3), .flip_mem(bus_encoder_1_flip_mem));
  // Probe on {register_controller_1_out_23, register_controller_1_out_22}
  // Probe on {register_controller_1_out_25, register_controller_1_out_24}
  Button button_1 (.out(button_1_out));
  LED led_1 (.in(memory_controller_1_not_shutdown));
  // Probe on register_controller_1_out_22
  // Probe on register_controller_1_out_23
  // Probe on register_controller_1_out_24
  // Probe on register_controller_1_out_25
  // Probe on register_controller_1_out_26
  // Probe on register_controller_1_out_27
  // Probe on stack_controller_1_stack_value
  // Probe on register_controller_1_out_29
  comparison_mux comparison_mux_1 (
    .in_1(register_controller_1_out_22), .in_2(register_controller_1_out_23),
    .in_3(register_controller_1_out_24), .in_4(register_controller_1_out_25),
    .in_5(register_controller_1_out_26), .in_6(register_controller_1_out_27),
    .in_7(stack_controller_1_stack_value), .in_8(register_controller_1_out_29),
    .comp_select(comparison_controller_1_cma_select), .out_10(comparison_mux_1_out_10));
  temp_gpu temp_gpu_1 (
    .data(memory_controller_1_ipba_data), .clock(controlled_buffer_1_out), .y_pos(temp_gpu_1_y_pos),
    .x_pos(temp_gpu_1_x_pos), .clock_out(temp_gpu_1_clock_out), .color(temp_gpu_1_color));
  // RGB_Video #(.cursor("No Cursor"), .height(64), .scale(4), .width(64)) rgb_video_1: pin names not known; wires that end beside it: temp_gpu_1_clock_out, 1'b1, temp_gpu_1_x_pos, temp_gpu_1_y_pos, temp_gpu_1_color
  // also tied to GND on the sheet: n74125_1_pin2
  // also tied to VCC on the sheet: n74163_1_pin7

  // Notes on the sheet:
  //   DEC
  //   HEX
  //   carry out
  //   AB
  //   CD
  //   Ext Int
  //   Power
  //   A
  //   B
  //   C
  //   D
  //   E
  //   F
  //   STP
  //   PC
endmodule

module gpu (
  input  [26:0] data,
  input  clock
);

  register_8 register_8_1 (.data(data[25:18]), .clken(data[26]), .clk(clock));  // open: out_4
  register_8 register_8_2 (.data(data[16:9]), .clken(data[17]), .clk(clock));  // open: out_4
  RAM #(.addrWidth(16)) ram_1 (.we(data[8]), .oe(1'b0), .clk(clock), .din(data[7:0]));  // open: addr, dout
endmodule

module temp_gpu (
  input  [26:0] data,
  input  clock,
  output [5:0] y_pos,
  output [5:0] x_pos,
  output clock_out,
  output [14:0] color
);

  wire [15:0] up_down_counter_16_1_count_out;
  wire [15:6] divider_1_out, divider_1_rem;

  Multiplier #(.width(5)) multiplier_1 (.a({2'b00, data[2:0]}), .b(5'b00100), .out(color[4:0]));  // open: cin, cout
  Multiplier #(.width(5)) multiplier_2 (.a({2'b00, data[5:3]}), .b(5'b00100), .out(color[9:5]));  // open: cin, cout
  Multiplier #(.width(5)) multiplier_3 (.a({3'b000, data[7:6]}), .b(5'b01000), .out(color[14:10]));  // open: cin, cout
  up_down_counter_16 up_down_counter_16_1 (
    .disable_lower(data[17]), .disable_upper(data[26]), .count_in({data[25:18], data[16:9]}),
    .not_count_down(1'b1), .not_count_up(data[8]), .count_out(up_down_counter_16_1_count_out));  // open: not_carry_out, not_borrow_out
  Divider #(.width(16)) divider_1 (
    .a(up_down_counter_16_1_count_out), .b(16'h40), .out({divider_1_out, y_pos}), .rem({divider_1_rem, x_pos}));  // open: upper

  assign clock_out = data[8];
endmodule

module memory_controller (
  input  [15:0] value_1,
  input  [15:0] value_2,
  input  [2:0] instruction_stage,
  input  not_carry_used,
  input  jump,
  input  not_carry_in,
  input  write_lower,
  input  write_upper,
  input  write_mem,
  input  read_mem,
  input  stack,
  input  compare,
  input  logical,
  input  compare_set,
  input  flip_mem,
  input  memory,
  input  simple,
  input  [7:0] operation_select,
  output [15:0] write_value,
  output carry_out,
  output not_shutdown,
  output [15:0] pic_a_address,
  output [7:0] pic_a_config,
  output [15:0] pic_b_address,
  output [7:0] pic_b_config,
  output [15:0] pic_c_address,
  output [7:0] pic_c_config,
  output [26:0] ipba_data,
  output [26:0] ipbb_data,
  output ps2a_rec,
  output ps2b_rec,
  output timera_ovf,
  output timerb_ovf
);

  wire n7432_1_pin3, n7432_1_pin4, n7432_1_pin6, n7432_1_pin11, not_1_out;
  wire [7:0] memory_module_1_read_value, tri_state_switch_8_3_out_3;

  // NoConnect on jump
  // NoConnect on write_lower
  // NoConnect on write_upper
  // NoConnect on stack
  // NoConnect on compare
  // NoConnect on logical
  // NoConnect on compare_set
  // NoConnect on simple
  not not_1 (not_1_out, flip_mem);
  tri_state_switch_8 tri_state_switch_8_1 (
    .a(memory_module_1_read_value), .disable_output(n7432_1_pin6), .out_3(write_value[7:0]));
  tri_state_switch_8 tri_state_switch_8_2 (
    .a(memory_module_1_read_value), .disable_output(n7432_1_pin3), .out_3(write_value[15:8]));
  _7432 u_7432_1 (
    .pin1(flip_mem), .pin2(read_mem), .pin3(n7432_1_pin3), .pin4(n7432_1_pin4), .pin5(read_mem),
    .pin6(n7432_1_pin6), .pin13(write_mem), .pin12(instruction_stage[1]), .pin11(n7432_1_pin11));  // open: pin10, pin9, pin8
  not not_2 (n7432_1_pin4, flip_mem);
  tri_state_switch_8 tri_state_switch_8_3 (
    .a(value_1[7:0]), .disable_output(not_1_out), .out_3(tri_state_switch_8_3_out_3));
  tri_state_switch_8 tri_state_switch_8_4 (
    .a(value_1[15:8]), .disable_output(flip_mem), .out_3(tri_state_switch_8_3_out_3));
  memory_module memory_module_1 (
    .address(value_2), .write_disable(n7432_1_pin11), .write_value(tri_state_switch_8_3_out_3),
    .output_disable(read_mem), .instruction_stage(instruction_stage), .not_carry_in(not_carry_in),
    .not_carry_used(not_carry_used), .read_value(memory_module_1_read_value), .carry_out(carry_out),
    .not_shutdown(not_shutdown), .ps2a_rec(ps2a_rec), .ps2b_rec(ps2b_rec), .pic_a_address(pic_a_address),
    .pic_a_config(pic_a_config), .pic_b_address(pic_b_address), .pic_b_config(pic_b_config),
    .pic_c_address(pic_c_address), .pic_c_config(pic_c_config), .ipba_data(ipba_data),
    .timera_ovf(timera_ovf), .timerb_ovf(timerb_ovf));  // open: ipbb_data
endmodule

module memory_module (
  input  [15:0] address,
  input  write_disable,
  input  [7:0] write_value,
  input  output_disable,
  input  [2:0] instruction_stage,
  input  not_carry_in,
  input  not_carry_used,
  output [7:0] read_value,
  output carry_out,
  output not_shutdown,
  output ps2a_rec,
  output ps2b_rec,
  output [15:0] pic_a_address,
  output [7:0] pic_a_config,
  output [15:0] pic_b_address,
  output [7:0] pic_b_config,
  output [15:0] pic_c_address,
  output [7:0] pic_c_config,
  output [26:0] ipba_data,
  output [26:0] ipbb_data,
  output timera_ovf,
  output timerb_ovf
);

  wire n7402_1_pin1, n7402_1_pin4, n7402_1_pin5, n7402_1_pin10, n7402_1_pin13, n7402_2_pin4, n7402_2_pin6,
       n7402_2_pin12, n7402_2_pin13, n7404_1_pin2, n7404_1_pin4, n7408_1_pin3, n7408_1_pin6,
       peripheral_controller_1_ipbb_send;

  _7402 u_7402_1 (
    .pin1(n7402_1_pin1), .pin2(address[15]), .pin3(output_disable), .pin4(n7402_1_pin4), .pin5(n7402_1_pin5),
    .pin6(output_disable), .pin13(n7402_1_pin13), .pin12(n7402_1_pin1), .pin11(n7402_1_pin1),
    .pin10(n7402_1_pin10), .pin9(n7402_1_pin4), .pin8(n7402_1_pin4));
  _7402 u_7402_2 (
    .pin1(n7402_1_pin5), .pin2(address[15]), .pin3(address[15]), .pin4(n7402_2_pin4), .pin5(write_disable),
    .pin6(n7402_2_pin6), .pin13(n7402_2_pin13), .pin12(n7402_2_pin12), .pin11(n7402_2_pin12),
    .pin10(n7402_2_pin12), .pin9(n7402_1_pin5), .pin8(write_disable));
  _7408 u_7408_1 (
    .pin1(address[12]), .pin2(address[13]), .pin3(n7408_1_pin3), .pin4(address[14]), .pin5(address[15]),
    .pin6(n7408_1_pin6), .pin10(n7408_1_pin3), .pin9(n7408_1_pin6), .pin8(n7402_2_pin6));  // open: pin13, pin12, pin11
  _7404 u_7404_1 (
    .pin1(n7402_2_pin4), .pin2(n7404_1_pin2), .pin3(n7402_2_pin6), .pin4(n7404_1_pin4));  // open: pin5, pin6, pin13, pin12, pin11, pin10, pin9, pin8
  rom_chip rom_chip_1 (
    .address(address[14:0]), .chip_disable(1'b0), .output_disable(n7402_1_pin13), .write_disable(1'b1),
    .io(read_value));
  ram_chip ram_chip_1 (
    .address(address[14:0]), .write_disable(n7404_1_pin2), .write_value(write_value),
    .output_disable(n7402_1_pin10), .read_value(read_value));
  peripheral_controller peripheral_controller_1 (
    .not_carry_in(not_carry_in), .not_carry_used(not_carry_used), .write_value(write_value),
    .output_disable(n7404_1_pin4), .write_disable(n7402_2_pin13), .instruction_stage(instruction_stage),
    .address(address), .pic_a_address(pic_a_address), .pic_a_config(pic_a_config),
    .pic_b_address(pic_b_address), .pic_b_config(pic_b_config), .pic_c_address(pic_c_address),
    .pic_c_config(pic_c_config), .carry_out(carry_out), .not_shutdown(not_shutdown), .read_value(read_value),
    .ipbb_send(peripheral_controller_1_ipbb_send), .int_ps2a_rec(ps2a_rec), .int_ps2b_rec(ps2b_rec),
    .timera_ovf(timera_ovf), .timerb_ovf(timerb_ovf), .ipba(ipba_data));  // open: ps2a_clk, ps2a_din
endmodule

module register_controller (
  input  in_1,
  input  [7:0] destination_register,
  input  [7:0] source_register,
  input  [15:0] write_value,
  input  [2:0] instruction_stage,
  input  jump,
  input  write_lower,
  input  write_upper,
  input  write_mem,
  input  read_mem,
  input  stack,
  input  compare,
  input  logical,
  input  compare_set,
  input  flip_mem,
  input  memory,
  input  simple,
  input  [7:0] operation_select,
  input  [15:0] pc,
  output [15:0] value_1,
  output [15:0] value_2,
  output [15:0] out_22,
  output [15:0] out_23,
  output [15:0] out_24,
  output [15:0] out_25,
  output [15:0] out_26,
  output [15:0] out_27,
  output stack_select_1,
  output [15:0] out_29,
  output stack_select_2
);

  wire n7432_1_pin8, n7432_1_pin11;

  // NoConnect on jump
  // NoConnect on write_mem
  // NoConnect on read_mem
  // NoConnect on stack
  // NoConnect on compare
  // NoConnect on logical
  // NoConnect on compare_set
  // NoConnect on flip_mem
  // NoConnect on memory
  // NoConnect on simple
  _7432 u_7432_1 (
    .pin13(write_lower), .pin12(instruction_stage[1]), .pin11(n7432_1_pin11), .pin10(write_upper),
    .pin9(instruction_stage[1]), .pin8(n7432_1_pin8));  // open: pin1, pin2, pin3, pin4, pin5, pin6
  main_register main_register_1 (
    .clock(in_1), .not_select_1(destination_register[0]), .not_select_2(source_register[0]),
    .write_value(write_value), .disable_upper(n7432_1_pin8), .disable_lower(n7432_1_pin11), .read_1(value_1),
    .read_2(value_2), .value(out_22));
  main_register main_register_2 (
    .clock(in_1), .not_select_1(destination_register[1]), .not_select_2(source_register[1]),
    .write_value(write_value), .disable_upper(n7432_1_pin8), .disable_lower(n7432_1_pin11), .read_1(value_1),
    .read_2(value_2), .value(out_23));
  main_register main_register_3 (
    .clock(in_1), .not_select_1(destination_register[2]), .not_select_2(source_register[2]),
    .write_value(write_value), .disable_upper(n7432_1_pin8), .disable_lower(n7432_1_pin11), .read_1(value_1),
    .read_2(value_2), .value(out_24));
  main_register main_register_4 (
    .clock(in_1), .not_select_1(destination_register[3]), .not_select_2(source_register[3]),
    .write_value(write_value), .disable_upper(n7432_1_pin8), .disable_lower(n7432_1_pin11), .read_1(value_1),
    .read_2(value_2), .value(out_25));
  main_register main_register_5 (
    .clock(in_1), .not_select_1(destination_register[4]), .not_select_2(source_register[4]),
    .write_value(write_value), .disable_upper(n7432_1_pin8), .disable_lower(n7432_1_pin11), .read_1(value_1),
    .read_2(value_2), .value(out_26));
  main_register main_register_6 (
    .clock(in_1), .not_select_1(destination_register[5]), .not_select_2(source_register[5]),
    .write_value(write_value), .disable_upper(n7432_1_pin8), .disable_lower(n7432_1_pin11), .read_1(value_1),
    .read_2(value_2), .value(out_27));
  tri_state_switch_16 tri_state_switch_16_1 (.a(pc), .disable_output(destination_register[7]), .out_3(value_1));
  tri_state_switch_16 tri_state_switch_16_2 (.a(pc), .disable_output(source_register[7]), .out_3(value_2));

  assign out_29 = pc;
  assign stack_select_1 = destination_register[6];
  assign stack_select_2 = source_register[6];
endmodule

module logical_controller (
  input  [15:0] value_1,
  input  [15:0] value_2,
  input  [2:0] instruction_stage,
  input  jump,
  input  write_lower,
  input  carry_in,
  input  write_upper,
  input  write_mem,
  input  read_mem,
  input  stack,
  input  compare,
  input  logical,
  input  compare_set,
  input  flip_mem,
  input  memory,
  input  simple,
  input  [7:0] operation_select,
  output [15:0] write_value,
  output not_carry_out,
  output not_carry_used
);

  wire alu_1_cout, n7404_1_pin4, n7404_1_pin6, n7404_1_pin9, n7404_1_pin11, n7408_1_pin3;
  wire [15:0] alu_1_o, and_16_1_out_3, not_16_1_out_2, or_16_1_out_3, tri_state_switch_16_2_out_3,
       xor_16_1_out_3;

  tri_state_switch_16 tri_state_switch_16_1 (
    .a(tri_state_switch_16_2_out_3), .disable_output(logical), .out_3(write_value));
  // NoConnect on jump
  // NoConnect on write_lower
  // NoConnect on write_upper
  // NoConnect on write_mem
  // NoConnect on read_mem
  // NoConnect on stack
  // NoConnect on compare
  // NoConnect on compare_set
  // NoConnect on flip_mem
  // NoConnect on memory
  // NoConnect on simple
  _7404 u_7404_1 (
    .pin3(operation_select[1]), .pin4(n7404_1_pin4), .pin5(logical), .pin6(n7404_1_pin6),
    .pin11(n7404_1_pin11), .pin10(not_carry_used), .pin9(n7404_1_pin9), .pin8(not_carry_out));  // open: pin1, pin2, pin13, pin12
  tri_state_switch_16 tri_state_switch_16_2 (
    .a(value_2), .disable_output(operation_select[0]), .out_3(tri_state_switch_16_2_out_3));
  alu alu_1 (.a(value_1), .b(value_2), .negate_b(operation_select[1]), .cin(carry_in), .o(alu_1_o), .cout(alu_1_cout));
  and_16 and_16_1 (.a(value_1), .b(value_2), .out_3(and_16_1_out_3));
  or_16 or_16_1 (.a(value_1), .b(value_2), .out_3(or_16_1_out_3));
  xor_16 xor_16_1 (.a(value_1), .b(value_2), .out_3(xor_16_1_out_3));
  not_16 not_16_1 (.in_1(value_1), .out_2(not_16_1_out_2));
  _7408 u_7408_1 (
    .pin1(operation_select[1]), .pin2(operation_select[2]), .pin3(n7408_1_pin3), .pin13(n7404_1_pin6),
    .pin12(n7404_1_pin4), .pin11(n7404_1_pin11), .pin10(n7404_1_pin11), .pin9(alu_1_cout), .pin8(n7404_1_pin9));  // open: pin4, pin5, pin6
  tri_state_switch_16 tri_state_switch_16_3 (
    .a(alu_1_o), .disable_output(n7408_1_pin3), .out_3(tri_state_switch_16_2_out_3));
  tri_state_switch_16 tri_state_switch_16_4 (
    .a(and_16_1_out_3), .disable_output(operation_select[3]), .out_3(tri_state_switch_16_2_out_3));
  tri_state_switch_16 tri_state_switch_16_5 (
    .a(or_16_1_out_3), .disable_output(operation_select[4]), .out_3(tri_state_switch_16_2_out_3));
  tri_state_switch_16 tri_state_switch_16_6 (
    .a(xor_16_1_out_3), .disable_output(operation_select[5]), .out_3(tri_state_switch_16_2_out_3));
  tri_state_switch_16 tri_state_switch_16_7 (
    .a(not_16_1_out_2), .disable_output(operation_select[6]), .out_3(tri_state_switch_16_2_out_3));
  tri_state_switch_16 tri_state_switch_16_8 (
    .a({value_1[0], value_1[15:1]}), .disable_output(operation_select[7]), .out_3(tri_state_switch_16_2_out_3));
endmodule

module comparison_controller (
  input  [2:0] destination_select,
  input  clock,
  input  [15:0] value_1,
  input  [15:0] value_2,
  input  [15:0] write_value,
  input  [2:0] instruction_stage,
  input  write_lower,
  input  write_upper,
  input  write_mem,
  input  read_mem,
  input  stack,
  input  compare,
  input  logical,
  input  compare_set,
  input  flip_mem,
  input  memory,
  input  simple,
  input  [7:0] operation_select,
  input  [15:0] comp_a,
  input  carry_in,
  output [2:0] cma_select,
  output jump
);

  wire logical_comparator_16_1_a_gt_b, logical_comparator_16_1_a_lt_b, n7408_1_pin3, n7408_1_pin4,
       n7408_1_pin6, n7414_1_pin2, n7414_1_pin4, n7414_1_pin8, n7414_1_pin10, n7414_1_pin12, n7427_1_pin3,
       n7427_1_pin6, n7427_1_pin8, n7427_1_pin12, n7427_2_pin12, n7432_1_pin3, n7432_1_pin6, n7432_1_pin8,
       n74125_1_pin3, n74125_1_pin12;
  wire [7:0] register_8_1_out_4, tri_state_switch_8_1_out_3;
  wire [7:3] register_8_2_out_4, undriven;
  wire [15:0] register_16_1_out_4, register_16_2_out_4, tri_state_switch_16_1_out_3;

  // NoConnect on value_2
  // NoConnect on write_value
  // NoConnect on write_lower
  // NoConnect on write_upper
  // NoConnect on write_mem
  // NoConnect on read_mem
  // NoConnect on stack
  // NoConnect on logical
  // NoConnect on flip_mem
  // NoConnect on memory
  _7432 u_7432_1 (
    .pin1(simple), .pin2(instruction_stage[1]), .pin3(n7432_1_pin3), .pin4(n7432_1_pin3),
    .pin5(operation_select[3]), .pin6(n7432_1_pin6), .pin10(n7432_1_pin3), .pin9(operation_select[4]),
    .pin8(n7432_1_pin8));  // open: pin13, pin12, pin11
  // NoConnect on operation_select[7]
  _7427 u_7427_1 (
    .pin1(instruction_stage[1]), .pin2(compare_set), .pin3(n7427_1_pin3), .pin4(n7427_1_pin3),
    .pin5(n7427_1_pin3), .pin6(n7427_1_pin6), .pin13(operation_select[1]), .pin12(n7427_1_pin12),
    .pin11(n7427_1_pin12), .pin10(n7427_1_pin12), .pin9(n7427_1_pin12), .pin8(n7427_1_pin8));
  _7408 u_7408_1 (
    .pin1(n7432_1_pin8), .pin2(n7427_1_pin8), .pin3(n7408_1_pin3), .pin4(n7408_1_pin4), .pin5(n7432_1_pin8),
    .pin6(n7408_1_pin6));  // open: pin13, pin12, pin11, pin10, pin9, pin8
  _7427 #(.ShowInternalStructure("true")) u_7427_2 (
    .pin1(instruction_stage[1]), .pin2(compare_set), .pin13(operation_select[0]), .pin12(n7427_2_pin12),
    .pin11(n7427_2_pin12), .pin10(n7427_2_pin12), .pin9(n7427_2_pin12), .pin8(n7408_1_pin4));  // open: pin3, pin4, pin5, pin6
  tri_state_switch_8 tri_state_switch_8_1 (
    .a({undriven, destination_select}), .disable_output(n7414_1_pin2), .out_3(tri_state_switch_8_1_out_3));
  logical_comparator_16 logical_comparator_16_1 (
    .A(comp_a), .B(register_16_1_out_4), .A_lt_B(logical_comparator_16_1_a_lt_b), .A_eq_B(n7427_1_pin3),
    .A_gt_B(logical_comparator_16_1_a_gt_b));
  tri_state_switch_16 tri_state_switch_16_1 (
    .a(value_1), .disable_output(n7414_1_pin2), .out_3(tri_state_switch_16_1_out_3));
  _7414 u_7414_1 (
    .pin1(n7432_1_pin8), .pin2(n7414_1_pin2), .pin3(n7432_1_pin6), .pin4(n7414_1_pin4),
    .pin13(logical_comparator_16_1_a_lt_b), .pin12(n7414_1_pin12), .pin11(logical_comparator_16_1_a_gt_b),
    .pin10(n7414_1_pin10), .pin9(carry_in), .pin8(n7414_1_pin8));  // open: pin5, pin6
  tri_state_switch_8 tri_state_switch_8_2 (
    .a(register_8_1_out_4), .disable_output(n7432_1_pin8), .out_3(tri_state_switch_8_1_out_3));
  _74125 #(.ShowInternalStructure("true")) u_74125_1 (
    .pin1(operation_select[2]), .pin2(n7427_1_pin3), .pin3(n74125_1_pin3), .pin4(operation_select[3]),
    .pin5(n7414_1_pin10), .pin6(n74125_1_pin3), .pin13(operation_select[0]), .pin12(n74125_1_pin12),
    .pin11(n74125_1_pin3), .pin10(operation_select[1]), .pin9(n7427_1_pin6), .pin8(n74125_1_pin3));
  _74125 #(.ShowInternalStructure("true")) u_74125_2 (
    .pin1(operation_select[6]), .pin2(carry_in), .pin3(n74125_1_pin3), .pin4(compare), .pin5(n74125_1_pin3),
    .pin6(jump), .pin13(operation_select[4]), .pin12(n7414_1_pin12), .pin11(n74125_1_pin3),
    .pin10(operation_select[5]), .pin9(n7414_1_pin8), .pin8(n74125_1_pin3));
  register_8 register_8_1 (
    .data({register_8_2_out_4, cma_select}), .clken(n7432_1_pin6), .clk(clock), .out_4(register_8_1_out_4));
  register_8 register_8_2 (
    .data(tri_state_switch_8_1_out_3), .clken(n7408_1_pin6), .clk(clock),
    .out_4({register_8_2_out_4, cma_select}));
  register_16 register_16_1 (
    .data(tri_state_switch_16_1_out_3), .clken(n7408_1_pin3), .clk(clock), .out_4(register_16_1_out_4));
  register_16 register_16_2 (
    .data(register_16_1_out_4), .clken(n7432_1_pin6), .clk(clock), .out_4(register_16_2_out_4));
  tri_state_switch_16 tri_state_switch_16_2 (
    .a(register_16_2_out_4), .disable_output(n7432_1_pin8), .out_3(tri_state_switch_16_1_out_3));
  // also tied to GND on the sheet: n74125_1_pin12
endmodule

module memory_access_controller (
  input  [15:0] value_1,
  input  [15:0] value_2,
  input  [2:0] instruction_stage,
  input  jump,
  input  write_lower,
  input  write_upper,
  input  stack,
  input  compare,
  input  logical,
  input  compare_set,
  input  memory,
  input  simple,
  input  [7:0] operation_select,
  output [15:0] write_value,
  output write_mem,
  output read_mem,
  output flip_mem
);

  wire n7432_1_pin2, n7432_1_pin3, n7432_1_pin4, n7432_1_pin6, n7432_1_pin8, n7432_1_pin9, n74125_1_pin2;

  // NoConnect on value_1
  tri_state_switch_16 tri_state_switch_16_1 (.a(value_2), .disable_output(n7432_1_pin6), .out_3(write_value));
  // NoConnect on jump
  // NoConnect on write_lower
  // NoConnect on write_upper
  // NoConnect on stack
  // NoConnect on compare
  _7432 u_7432_1 (
    .pin1(memory), .pin2(n7432_1_pin2), .pin3(n7432_1_pin3), .pin4(n7432_1_pin4), .pin5(memory),
    .pin6(n7432_1_pin6), .pin10(memory), .pin9(n7432_1_pin9), .pin8(n7432_1_pin8));  // open: pin13, pin12, pin11
  // NoConnect on logical
  // NoConnect on compare_set
  // NoConnect on simple
  _74125 #(.ShowInternalStructure("true")) u_74125_1 (
    .pin1(n7432_1_pin8), .pin2(n74125_1_pin2), .pin3(read_mem), .pin4(n7432_1_pin6), .pin5(n74125_1_pin2),
    .pin6(write_mem), .pin10(n7432_1_pin3), .pin9(n74125_1_pin2), .pin8(flip_mem));  // open: pin13, pin12, pin11
  // NoConnect on operation_select[7]
  _7408 u_7408_1 (
    .pin1(operation_select[1]), .pin2(operation_select[3]), .pin3(n7432_1_pin2), .pin4(operation_select[0]),
    .pin5(operation_select[1]), .pin6(n7432_1_pin4), .pin10(operation_select[3]), .pin9(operation_select[2]),
    .pin8(n7432_1_pin9));  // open: pin13, pin12, pin11
  // also tied to GND on the sheet: n74125_1_pin2
endmodule

module stack_controller (
  input  stack_select_1,
  input  stack_select_2,
  input  [15:0] write_value,
  input  [2:0] instruction_stage,
  input  jump,
  input  write_lower,
  input  write_upper,
  input  stack,
  input  compare,
  input  logical,
  input  compare_set,
  input  memory,
  input  simple,
  input  [7:0] operation_select,
  output [15:0] stack_value,
  output [15:0] value_1,
  output [15:0] value_2,
  output write_mem,
  output read_mem,
  output flip_mem
);

  wire n7408_1_pin3, n7408_1_pin6, n7408_1_pin11, n7408_1_pin13, n7408_2_pin3, n7408_2_pin11, n7432_1_pin1,
       n7432_1_pin3, n7432_1_pin5, n7432_1_pin6, n7432_2_pin11, n7432_3_pin11, n74125_1_pin1, n74125_1_pin2,
       n74125_1_pin4, n74125_1_pin10;
  wire [15:0] register_16_1_out_4;

  // NoConnect on jump
  // NoConnect on compare
  // NoConnect on logical
  // NoConnect on compare_set
  // NoConnect on memory
  // NoConnect on simple
  // NoConnect on operation_select[7]
  _7432 u_7432_1 (
    .pin1(n7432_1_pin1), .pin2(instruction_stage[1]), .pin3(n7432_1_pin3), .pin4(instruction_stage[1]),
    .pin5(n7432_1_pin5), .pin6(n7432_1_pin6), .pin13(write_lower), .pin12(stack_select_1),
    .pin11(n7432_1_pin1), .pin10(write_upper), .pin9(stack_select_1), .pin8(n7432_1_pin5));
  _74125 #(.ShowInternalStructure("true")) u_74125_1 (
    .pin1(n74125_1_pin1), .pin2(n74125_1_pin2), .pin3(write_mem), .pin4(n74125_1_pin4), .pin5(n74125_1_pin2),
    .pin6(read_mem), .pin10(n74125_1_pin10), .pin9(n74125_1_pin2), .pin8(flip_mem));  // open: pin13, pin12, pin11
  register_16 register_16_1 (
    .data(write_value), .clken(n7408_2_pin11), .clk(instruction_stage[0]), .out_4(register_16_1_out_4));
  _7408 u_7408_1 (
    .pin1(operation_select[0]), .pin2(operation_select[1]), .pin3(n7408_1_pin3), .pin4(operation_select[1]),
    .pin5(operation_select[3]), .pin6(n7408_1_pin6), .pin13(n7408_1_pin13), .pin12(stack_select_2),
    .pin11(n7408_1_pin11), .pin10(n74125_1_pin1), .pin9(n74125_1_pin4), .pin8(n7408_1_pin13));
  _7432 u_7432_2 (
    .pin1(stack), .pin2(n7408_1_pin3), .pin3(n74125_1_pin1), .pin4(n7408_1_pin6), .pin5(stack),
    .pin6(n74125_1_pin10), .pin13(n74125_1_pin1), .pin12(instruction_stage[2]), .pin11(n7432_2_pin11));  // open: pin10, pin9, pin8
  up_down_counter_16 up_down_counter_16_1 (
    .disable_lower(n7432_1_pin3), .disable_upper(n7432_1_pin6), .count_in(register_16_1_out_4),
    .not_count_down(n7432_3_pin11), .not_count_up(n7432_2_pin11), .count_out(stack_value));  // open: not_carry_out, not_borrow_out
  _7408 u_7408_2 (
    .pin1(operation_select[2]), .pin2(operation_select[3]), .pin3(n7408_2_pin3), .pin13(write_upper),
    .pin12(write_lower), .pin11(n7408_2_pin11));  // open: pin4, pin5, pin6, pin10, pin9, pin8
  tri_state_switch_16 tri_state_switch_16_1 (.a(stack_value), .disable_output(stack_select_1), .out_3(value_1));
  tri_state_switch_16 tri_state_switch_16_2 (.a(stack_value), .disable_output(n7408_1_pin11), .out_3(value_2));
  _7432 u_7432_3 (
    .pin1(stack), .pin2(n7408_2_pin3), .pin3(n74125_1_pin4), .pin13(n74125_1_pin4),
    .pin12(instruction_stage[0]), .pin11(n7432_3_pin11));  // open: pin4, pin5, pin6, pin10, pin9, pin8
  // also tied to GND on the sheet: n74125_1_pin2
endmodule

module interrupt_controller (
  input  ext,
  input  a,
  input  b,
  input  ps2a,
  input  ps2b,
  input  timera,
  input  timerb,
  input  [7:0] pic_a_config,
  input  [7:0] pic_b_config,
  input  [7:0] pic_c_config,
  input  [15:0] pic_a_address,
  input  [15:0] pic_b_address,
  input  [15:0] pic_c_address,
  input  [15:0] value_1,
  input  [15:0] value_2,
  input  [2:0] instruction_stage,
  input  jump,
  input  write_lower,
  input  write_upper,
  input  write_mem,
  input  read_mem,
  input  stack,
  input  compare,
  input  logical,
  input  compare_set,
  input  flip_mem,
  input  interrupt_stage,
  input  memory,
  input  simple,
  input  [7:0] operation_select,
  input  [15:0] program_counter,
  output not_jump,
  output [15:0] jump_address,
  output [15:0] write_value
);

  wire n7404_1_pin2, n7404_1_pin4, n7404_1_pin6, n7404_1_pin8, n7404_1_pin10, n7404_1_pin12, n7404_2_pin2,
       n7404_2_pin4, n7404_2_pin6, n7404_2_pin8, n7404_2_pin10, n7404_2_pin12, n7404_3_pin2, n7404_3_pin4,
       n7404_3_pin6, n7404_3_pin8, n7404_3_pin10, n7404_3_pin12, n7404_4_pin2, n7404_4_pin4, n7404_4_pin6,
       n7404_4_pin8, n7404_4_pin10, n7404_4_pin12, n7408_1_pin3, n7432_1_pin3, n7432_1_pin6, n7432_2_pin3,
       n7432_2_pin6, n7432_2_pin8, n7432_2_pin11, n7432_3_pin3, n7432_3_pin5, n7432_3_pin6, n7432_3_pin8,
       n7432_3_pin11, n7432_4_pin3, n7432_4_pin6, n7432_4_pin8, n7432_4_pin11, n7432_5_pin3, n7432_5_pin8,
       n7432_5_pin11, n7432_6_pin3, n7432_6_pin6, n7432_6_pin8, n7432_6_pin11, n7432_7_pin3, n7432_7_pin8,
       n7432_7_pin11, n7474_1_pin4, n7474_1_pin5, n7474_1_pin8, n7474_1_pin10, not_1_out,
       pic_controller_1_jump, pic_controller_2_jump, pic_controller_3_jump;
  wire [3:0] register_16_1_out_4, register_16_1_out_4_2, register_16_1_out_4_3, register_16_1_out_4_4;
  wire [6:0] input_buffer_8_1_out_16;
  wire [15:0] mux_16_1_o, mux_16_2_o, mux_16_3_o;

  // NoConnect on jump
  // NoConnect on write_lower
  // NoConnect on write_upper
  // NoConnect on write_mem
  // NoConnect on read_mem
  // NoConnect on stack
  // NoConnect on compare
  // NoConnect on logical
  // NoConnect on compare_set
  // NoConnect on flip_mem
  // NoConnect on memory
  _7432 u_7432_1 (
    .pin1(simple), .pin2(operation_select[2]), .pin3(n7432_1_pin3), .pin4(n7432_1_pin3),
    .pin5(instruction_stage[0]), .pin6(n7432_1_pin6));  // open: pin13, pin12, pin11, pin10, pin9, pin8
  input_buffer_8 input_buffer_8_1 (
    .in_1(ext), .in_2(a), .in_3(b), .in_4(ps2a), .in_5(ps2b), .in_6(timera), .in_7(timerb),
    .not_clear(n7432_1_pin6), .out_10(input_buffer_8_1_out_16[6]), .out_11(input_buffer_8_1_out_16[5]),
    .out_12(input_buffer_8_1_out_16[4]), .out_13(input_buffer_8_1_out_16[3]),
    .out_14(input_buffer_8_1_out_16[2]), .out_15(input_buffer_8_1_out_16[1]),
    .out_16(input_buffer_8_1_out_16[0]));  // open: in_8, out_17
  _7404 #(.ShowInternalStructure("true")) u_7404_1 (
    .pin1(pic_b_config[1]), .pin2(n7404_1_pin2), .pin3(pic_b_config[0]), .pin4(n7404_1_pin4),
    .pin5(pic_b_config[3]), .pin6(n7404_1_pin6), .pin13(pic_a_config[7]), .pin12(n7404_1_pin12),
    .pin11(pic_a_config[6]), .pin10(n7404_1_pin10), .pin9(pic_b_config[2]), .pin8(n7404_1_pin8));
  _7404 #(.ShowInternalStructure("true")) u_7404_2 (
    .pin1(pic_a_config[4]), .pin2(n7404_2_pin2), .pin3(pic_a_config[5]), .pin4(n7404_2_pin4),
    .pin5(pic_a_config[0]), .pin6(n7404_2_pin6), .pin13(pic_a_config[3]), .pin12(n7404_2_pin12),
    .pin11(pic_a_config[2]), .pin10(n7404_2_pin10), .pin9(pic_a_config[1]), .pin8(n7404_2_pin8));
  _7404 #(.ShowInternalStructure("true")) u_7404_3 (
    .pin1(pic_c_config[1]), .pin2(n7404_3_pin2), .pin3(pic_c_config[2]), .pin4(n7404_3_pin4),
    .pin5(pic_b_config[6]), .pin6(n7404_3_pin6), .pin13(pic_b_config[7]), .pin12(n7404_3_pin12),
    .pin11(pic_b_config[4]), .pin10(n7404_3_pin10), .pin9(pic_b_config[5]), .pin8(n7404_3_pin8));
  _7404 #(.ShowInternalStructure("true")) u_7404_4 (
    .pin1(pic_c_config[6]), .pin2(n7404_4_pin2), .pin3(pic_c_config[7]), .pin4(n7404_4_pin4),
    .pin5(pic_c_config[0]), .pin6(n7404_4_pin6), .pin13(pic_c_config[3]), .pin12(n7404_4_pin12),
    .pin11(pic_c_config[4]), .pin10(n7404_4_pin10), .pin9(pic_c_config[5]), .pin8(n7404_4_pin8));
  LED #(.active("false")) led_1 (.in(input_buffer_8_1_out_16[6]));
  Pull_Resistor #(.pull(1)) pull_resistor_1 (.node(input_buffer_8_1_out_16[6]));
  LED #(.active("false")) led_2 (.in(input_buffer_8_1_out_16[5]));
  LED #(.active("false")) led_3 (.in(input_buffer_8_1_out_16[3]));
  LED #(.active("false")) led_4 (.in(input_buffer_8_1_out_16[1]));
  LED #(.active("false")) led_5 (.in(input_buffer_8_1_out_16[4]));
  LED #(.active("false")) led_6 (.in(input_buffer_8_1_out_16[2]));
  LED #(.active("false")) led_7 (.in(input_buffer_8_1_out_16[0]));
  Pull_Resistor #(.pull(1)) pull_resistor_2 (.node(input_buffer_8_1_out_16[5]));
  Pull_Resistor #(.pull(1)) pull_resistor_3 (.node(input_buffer_8_1_out_16[4]));
  Pull_Resistor #(.pull(1)) pull_resistor_4 (.node(input_buffer_8_1_out_16[3]));
  Pull_Resistor #(.pull(1)) pull_resistor_5 (.node(input_buffer_8_1_out_16[2]));
  Pull_Resistor #(.pull(1)) pull_resistor_6 (.node(input_buffer_8_1_out_16[1]));
  Pull_Resistor #(.pull(1)) pull_resistor_7 (.node(input_buffer_8_1_out_16[0]));
  _7432 u_7432_2 (
    .pin1(input_buffer_8_1_out_16[3]), .pin2(n7404_2_pin2), .pin3(n7432_2_pin3),
    .pin4(input_buffer_8_1_out_16[4]), .pin5(n7404_2_pin12), .pin6(n7432_2_pin6),
    .pin13(input_buffer_8_1_out_16[6]), .pin12(n7404_2_pin8), .pin11(n7432_2_pin11),
    .pin10(input_buffer_8_1_out_16[5]), .pin9(n7404_2_pin10), .pin8(n7432_2_pin8));
  _7432 #(.ShowInternalStructure("true")) u_7432_3 (
    .pin1(input_buffer_8_1_out_16[0]), .pin2(n7404_1_pin12), .pin3(n7432_3_pin3), .pin4(interrupt_stage),
    .pin5(n7432_3_pin5), .pin6(n7432_3_pin6), .pin13(input_buffer_8_1_out_16[1]), .pin12(n7404_1_pin10),
    .pin11(n7432_3_pin11), .pin10(input_buffer_8_1_out_16[2]), .pin9(n7404_2_pin4), .pin8(n7432_3_pin8));
  _7432 u_7432_4 (
    .pin1(input_buffer_8_1_out_16[4]), .pin2(n7404_1_pin6), .pin3(n7432_4_pin3),
    .pin4(input_buffer_8_1_out_16[3]), .pin5(n7404_3_pin10), .pin6(n7432_4_pin6), .pin13(n7404_1_pin2),
    .pin12(input_buffer_8_1_out_16[6]), .pin11(n7432_4_pin11), .pin10(input_buffer_8_1_out_16[5]),
    .pin9(n7404_1_pin8), .pin8(n7432_4_pin8));
  _7432 u_7432_5 (
    .pin1(n7404_3_pin12), .pin2(input_buffer_8_1_out_16[0]), .pin3(n7432_5_pin3), .pin13(n7404_3_pin6),
    .pin12(input_buffer_8_1_out_16[1]), .pin11(n7432_5_pin11), .pin10(n7404_3_pin8),
    .pin9(input_buffer_8_1_out_16[2]), .pin8(n7432_5_pin8));  // open: pin4, pin5, pin6
  _7432 u_7432_6 (
    .pin1(n7404_4_pin12), .pin2(input_buffer_8_1_out_16[4]), .pin3(n7432_6_pin3), .pin4(n7404_4_pin10),
    .pin5(input_buffer_8_1_out_16[3]), .pin6(n7432_6_pin6), .pin13(n7404_3_pin2),
    .pin12(input_buffer_8_1_out_16[6]), .pin11(n7432_6_pin11), .pin10(n7404_3_pin4),
    .pin9(input_buffer_8_1_out_16[5]), .pin8(n7432_6_pin8));
  _7432 u_7432_7 (
    .pin1(n7404_4_pin4), .pin2(input_buffer_8_1_out_16[0]), .pin3(n7432_7_pin3), .pin13(n7404_4_pin8),
    .pin12(input_buffer_8_1_out_16[2]), .pin11(n7432_7_pin11), .pin10(n7404_4_pin2),
    .pin9(input_buffer_8_1_out_16[1]), .pin8(n7432_7_pin8));  // open: pin4, pin5, pin6
  _7474 #(.ShowInternalStructure("true")) u_7474_1 (
    .pin1(n7432_1_pin6), .pin4(n7474_1_pin4), .pin5(n7474_1_pin5), .pin13(n7474_1_pin4),
    .pin10(n7474_1_pin10), .pin8(n7474_1_pin8));  // open: pin2, pin3, pin6, pin12, pin11, pin9
  pic_controller pic_controller_1 (
    .not_enable(n7404_2_pin6), .not_ext(n7432_2_pin11), .not_a(n7432_2_pin8), .not_b(n7432_2_pin6),
    .not_ps2a(n7432_2_pin3), .not_ps2b(n7432_3_pin11), .not_timera(n7432_3_pin8), .not_timerb(n7432_3_pin3),
    .jump(pic_controller_1_jump));
  pic_controller pic_controller_2 (
    .not_enable(n7404_1_pin4), .not_ext(n7432_4_pin11), .not_a(n7432_4_pin8), .not_b(n7432_4_pin3),
    .not_ps2a(n7432_4_pin6), .not_ps2b(n7432_5_pin8), .not_timera(n7432_5_pin11), .not_timerb(n7432_5_pin3),
    .jump(pic_controller_2_jump));
  pic_controller pic_controller_3 (
    .not_enable(n7404_4_pin6), .not_ext(n7432_6_pin11), .not_a(n7432_6_pin8), .not_b(n7432_6_pin3),
    .not_ps2a(n7432_6_pin6), .not_ps2b(n7432_7_pin11), .not_timera(n7432_7_pin8), .not_timerb(n7432_7_pin3),
    .jump(pic_controller_3_jump));
  LED led_8 (.in(n7474_1_pin5));
  _7408 u_7408_1 (
    .pin1(pic_controller_1_jump), .pin2(pic_controller_2_jump), .pin3(n7408_1_pin3), .pin4(n7408_1_pin3),
    .pin5(pic_controller_3_jump), .pin6(n7432_3_pin5), .pin10(n7432_1_pin6), .pin9(n7474_1_pin10),
    .pin8(not_jump));  // open: pin13, pin12, pin11
  _7432 u_7432_8 (
    .pin1(n7474_1_pin5), .pin2(n7432_3_pin6), .pin3(n7474_1_pin10), .pin13(instruction_stage[0]),
    .pin12(n7474_1_pin8), .pin11(n7474_1_pin4));  // open: pin4, pin5, pin6, pin10, pin9, pin8
  not not_1 (not_1_out, n7474_1_pin10);
  mux_16 mux_16_1 (.a(pic_b_address), .b(pic_c_address), .ab(pic_controller_2_jump), .o(mux_16_1_o));
  Hex_Digit_Display hex_digit_display_1 (.value(register_16_1_out_4_4));  // open: dp
  register_16 register_16_1 (
    .data(program_counter), .clken(1'b0), .clk(not_1_out),
    .out_4({register_16_1_out_4_4, register_16_1_out_4_3, register_16_1_out_4_2, register_16_1_out_4}));
  Hex_Digit_Display hex_digit_display_2 (.value(register_16_1_out_4_3));  // open: dp
  Hex_Digit_Display hex_digit_display_3 (.value(register_16_1_out_4_2));  // open: dp
  Hex_Digit_Display hex_digit_display_4 (.value(register_16_1_out_4));  // open: dp
  mux_16 mux_16_2 (.a(pic_a_address), .b(mux_16_1_o), .ab(pic_controller_1_jump), .o(mux_16_2_o));
  mux_16 mux_16_3 (
    .a({register_16_1_out_4_4, register_16_1_out_4_3, register_16_1_out_4_2, register_16_1_out_4}),
    .b(mux_16_2_o), .ab(n7432_1_pin6), .o(mux_16_3_o));
  tri_state_switch_16 tri_state_switch_16_1 (.a(mux_16_3_o), .disable_output(not_jump), .out_3(jump_address));

  // Notes on the sheet:
  //   simple: initial=0x1
endmodule

module pic_controller (
  input  not_enable,
  input  not_ext,
  input  not_a,
  input  not_b,
  input  not_ps2a,
  input  not_ps2b,
  input  not_timera,
  input  not_timerb,
  output jump
);

  wire n7421_1_pin6, n74244_1_pin3, n74244_1_pin5, n74244_1_pin7, n74244_1_pin9, n74244_1_pin14,
       n74244_1_pin16, n74244_1_pin18;

  _74244 #(.ShowInternalStructure("true")) u_74244_1 (
    .pin1(not_enable), .pin2(not_ps2b), .pin3(n74244_1_pin3), .pin4(not_timera), .pin5(n74244_1_pin5),
    .pin6(not_timerb), .pin7(n74244_1_pin7), .pin9(n74244_1_pin9), .pin19(not_enable),
    .pin18(n74244_1_pin18), .pin17(not_ps2a), .pin16(n74244_1_pin16), .pin15(not_b), .pin14(n74244_1_pin14),
    .pin13(not_a), .pin11(not_ext));  // open: pin8, pin12
  Pull_Resistor #(.pull(1)) pull_resistor_1 (.node(n74244_1_pin9));
  Pull_Resistor #(.pull(1)) pull_resistor_2 (.node(n74244_1_pin7));
  Pull_Resistor #(.pull(1)) pull_resistor_3 (.node(n74244_1_pin5));
  Pull_Resistor #(.pull(1)) pull_resistor_4 (.node(n74244_1_pin3));
  Pull_Resistor #(.pull(1)) pull_resistor_5 (.node(n74244_1_pin18));
  Pull_Resistor #(.pull(1)) pull_resistor_6 (.node(n74244_1_pin16));
  Pull_Resistor #(.pull(1)) pull_resistor_7 (.node(n74244_1_pin14));
  _7421 #(.ShowInternalStructure("true")) u_7421_1 (
    .pin1(n74244_1_pin3), .pin2(n74244_1_pin18), .pin4(n74244_1_pin16), .pin5(n74244_1_pin14),
    .pin6(n7421_1_pin6), .pin13(n74244_1_pin5), .pin12(n74244_1_pin7), .pin10(n74244_1_pin9),
    .pin9(n7421_1_pin6), .pin8(jump));  // open: pin3, pin11
endmodule

module peripheral_controller (
  input  [15:0] address,
  input  [7:0] write_value,
  input  output_disable,
  input  write_disable,
  input  [2:0] instruction_stage,
  input  not_carry_in,
  input  not_carry_used,
  input  ps2a_clk,
  input  ps2a_din,
  output [7:0] read_value,
  output carry_out,
  output not_shutdown,
  output [26:0] ipba,
  output ipbb_send,
  output int_ps2a_rec,
  output [15:0] pic_a_address,
  output int_ps2b_rec,
  output [7:0] pic_a_config,
  output timera_ovf,
  output timerb_ovf,
  output [15:0] pic_b_address,
  output [7:0] pic_b_config,
  output [15:0] pic_c_address,
  output [7:0] pic_c_config
);

  wire n7404_1_pin6, n7404_1_pin8, n7404_1_pin9, n7404_1_pin10, n7404_1_pin11, n7410_1_pin1, n7410_1_pin5,
       n7410_1_pin6, n7432_1_pin3, n7432_1_pin6, n7432_1_pin8, n7432_2_pin4, n7432_2_pin8, n7432_3_pin3,
       n7432_3_pin8, n7474_1_pin1, n7474_1_pin5, n7474_2_pin5, n7474_2_pin13, n74163_1_pin1, n74163_1_pin7,
       n74163_1_pin11, n74164_2_pin8;
  wire [7:0] n74164_2_pin3;
  wire [31:0] switched_decoder_5_1_out_3;

  _7410 #(.ShowInternalStructure("true")) u_7410_1 (
    .pin1(n7410_1_pin1), .pin2(n7410_1_pin1), .pin3(address[12]), .pin4(address[12]), .pin5(n7410_1_pin5),
    .pin6(n7410_1_pin6), .pin13(n7410_1_pin1), .pin12(n7410_1_pin5), .pin11(address[13]),
    .pin10(address[14]), .pin9(address[15]), .pin8(n7410_1_pin1));
  switched_decoder_5 switched_decoder_5_1 (
    .in_1(address[4:0]), .chip_disable(n7410_1_pin6), .out_3(switched_decoder_5_1_out_3));
  _7432 u_7432_1 (
    .pin1(instruction_stage[2]), .pin2(switched_decoder_5_1_out_3[3]), .pin3(n7432_1_pin3),
    .pin4(switched_decoder_5_1_out_3[0]), .pin5(output_disable), .pin6(n7432_1_pin6),
    .pin13(switched_decoder_5_1_out_3[6]), .pin12(instruction_stage[2]), .pin11(ipbb_send),
    .pin10(write_disable), .pin9(switched_decoder_5_1_out_3[0]), .pin8(n7432_1_pin8));
  _7432 u_7432_2 (
    .pin1(n7432_1_pin3), .pin2(write_disable), .pin3(ipba[8]), .pin4(n7432_2_pin4), .pin5(write_disable),
    .pin6(ipba[17]), .pin13(switched_decoder_5_1_out_3[2]), .pin12(instruction_stage[2]),
    .pin11(n7432_2_pin4), .pin10(switched_decoder_5_1_out_3[1]), .pin9(instruction_stage[2]),
    .pin8(n7432_2_pin8));
  _7404 u_7404_1 (
    .pin5(write_value[2]), .pin6(n7404_1_pin6), .pin11(n7404_1_pin11), .pin10(n7404_1_pin10),
    .pin9(n7404_1_pin9), .pin8(n7404_1_pin8));  // open: pin1, pin2, pin3, pin4, pin13, pin12
  _7432 u_7432_3 (
    .pin1(switched_decoder_5_1_out_3[0]), .pin2(write_disable), .pin3(n7432_3_pin3), .pin4(n7404_1_pin6),
    .pin5(n7432_3_pin3), .pin6(not_shutdown), .pin13(instruction_stage[2]), .pin12(not_carry_used),
    .pin11(n7404_1_pin9), .pin10(not_carry_used), .pin9(n7404_1_pin10), .pin8(n7432_3_pin8));
  _7432 u_7432_4 (
    .pin13(n7432_2_pin8), .pin12(write_disable), .pin11(ipba[26]));  // open: pin1, pin2, pin3, pin4, pin5, pin6, pin10, pin9, pin8
  register_8 register_8_1 (.clken(switched_decoder_5_1_out_3[9]), .clk(instruction_stage[1]));  // open: data, out_4
  register_8 register_8_2 (.clken(switched_decoder_5_1_out_3[10]), .clk(instruction_stage[1]));  // open: data, out_4
  register_8 register_8_3 (.clken(switched_decoder_5_1_out_3[11]), .clk(instruction_stage[1]));  // open: data, out_4
  register_8 register_8_4 (.clken(switched_decoder_5_1_out_3[12]), .clk(instruction_stage[1]));  // open: data, out_4
  register_8 register_8_5 (
    .data(write_value), .clken(switched_decoder_5_1_out_3[13]), .clk(instruction_stage[1]),
    .out_4(pic_a_address[15:8]));
  register_8 register_8_6 (
    .data(write_value), .clken(switched_decoder_5_1_out_3[14]), .clk(instruction_stage[1]),
    .out_4(pic_a_address[7:0]));
  register_8 register_8_7 (
    .data(write_value), .clken(switched_decoder_5_1_out_3[15]), .clk(instruction_stage[1]),
    .out_4(pic_a_config));
  register_8 register_8_8 (
    .data(write_value), .clken(switched_decoder_5_1_out_3[16]), .clk(instruction_stage[1]),
    .out_4(pic_b_address[15:8]));
  register_8 register_8_9 (
    .data(write_value), .clken(switched_decoder_5_1_out_3[17]), .clk(instruction_stage[1]),
    .out_4(pic_b_address[7:0]));
  register_8 register_8_10 (
    .data(write_value), .clken(switched_decoder_5_1_out_3[18]), .clk(instruction_stage[1]),
    .out_4(pic_b_config));
  register_8 register_8_11 (
    .data(write_value), .clken(switched_decoder_5_1_out_3[19]), .clk(instruction_stage[1]),
    .out_4(pic_c_address[15:8]));
  register_8 register_8_12 (
    .data(write_value), .clken(switched_decoder_5_1_out_3[20]), .clk(instruction_stage[1]),
    .out_4(pic_c_address[7:0]));
  register_8 register_8_13 (
    .data(write_value), .clken(switched_decoder_5_1_out_3[21]), .clk(instruction_stage[1]),
    .out_4(pic_c_config));
  _7474 #(.ShowInternalStructure("true")) u_7474_1 (
    .pin1(n7474_1_pin1), .pin2(write_value[1]), .pin3(n7432_1_pin8), .pin4(n7474_1_pin1), .pin5(n7474_1_pin5));  // open: pin6, pin13, pin12, pin11, pin10, pin9, pin8
  _7474 #(.ShowInternalStructure("true")) u_7474_2 (
    .pin1(n7432_3_pin8), .pin2(write_value[0]), .pin3(n7432_1_pin8), .pin4(n7404_1_pin11),
    .pin5(n7474_2_pin5), .pin13(n7474_2_pin13), .pin12(n7474_2_pin5), .pin11(n7404_1_pin8),
    .pin10(n7474_2_pin13), .pin9(carry_out));  // open: pin6, pin8
  _74125 #(.ShowInternalStructure("true")) u_74125_1 (
    .pin1(n7432_1_pin6), .pin2(carry_out), .pin3(read_value[0]), .pin4(n7432_1_pin6), .pin5(n7474_1_pin5),
    .pin6(read_value[1]), .pin13(n7474_1_pin5), .pin12(not_carry_in), .pin11(n7404_1_pin11));  // open: pin10, pin9, pin8
  Pull_Resistor #(.pull(1)) pull_resistor_1 (.node(n7404_1_pin11));
  _74164 #(.ShowInternalStructure("true")) u_74164_1 ();  // open: pin1, pin2, pin3, pin4, pin5, pin6, pin13, pin12, pin11, pin10, pin9, pin8
  _74164 #(.ShowInternalStructure("true")) u_74164_2 (
    .pin1(ps2a_din), .pin2(ps2a_din), .pin3(n74164_2_pin3[0]), .pin4(n74164_2_pin3[1]),
    .pin5(n74164_2_pin3[2]), .pin6(n74164_2_pin3[3]), .pin13(n74164_2_pin3[7]), .pin12(n74164_2_pin3[6]),
    .pin11(n74164_2_pin3[5]), .pin10(n74164_2_pin3[4]), .pin8(n74164_2_pin8));  // open: pin9
  _74163 #(.ShowInternalStructure("true")) u_74163_1 (
    .pin1(n74163_1_pin1), .pin2(n74164_2_pin8), .pin7(n74163_1_pin7), .pin11(n74163_1_pin11),
    .pin10(n74163_1_pin7), .pin9(n74163_1_pin7));  // open: pin3, pin4, pin5, pin6, pin15, pin14, pin13, pin12
  _7404 u_7404_2 (
    .pin1(ps2a_clk), .pin2(n74164_2_pin8), .pin13(n74163_1_pin11), .pin12(n74163_1_pin1));  // open: pin3, pin4, pin5, pin6, pin11, pin10, pin9, pin8
  register_8 register_8_14 (
    .data(write_value), .clken(switched_decoder_5_1_out_3[1]), .clk(instruction_stage[0]), .out_4(ipba[25:18]));
  register_8 register_8_15 (
    .data(write_value), .clken(switched_decoder_5_1_out_3[2]), .clk(instruction_stage[0]), .out_4(ipba[16:9]));
  register_8 register_8_16 (
    .data(write_value), .clken(switched_decoder_5_1_out_3[4]), .clk(instruction_stage[0]));  // open: out_4
  register_8 register_8_17 (
    .data(write_value), .clken(switched_decoder_5_1_out_3[5]), .clk(instruction_stage[0]));  // open: out_4
  register_8 register_8_18 (
    .data(write_value), .clken(switched_decoder_5_1_out_3[6]), .clk(instruction_stage[0]));  // open: out_4

  assign ipba[7:0] = write_value;
  // also tied to VCC on the sheet: {n7474_2_pin13, n7474_1_pin1, n74163_1_pin7}

  // Notes on the sheet:
  //   not_carry_in: initial=0x1
  //   flags register
  //   pbus
  //   timer
  //   pic
endmodule

module rom_chip (
  input  [14:0] address,
  input  chip_disable,
  input  output_disable,
  input  write_disable,
  output [7:0] io
);

  wire and_1_out, not_1_out, not_2_out;
  wire [7:0] rom_1_data;

  ROM #(.addrWidth(15)) rom_1 (.addr(address), .data(rom_1_data));
  assign io = and_1_out ? rom_1_data : 8'bz;  // Controlled_Buffer controlled_buffer_1
  not not_1 (not_1_out, chip_disable);
  not not_2 (not_2_out, output_disable);
  and and_1 (and_1_out, not_1_out, not_2_out, write_disable);

  // Notes on the sheet:
  //   contents of rom_1 (hex, n*v repeats v):
  //   ce 80 c6 0 d0 2 c9 f0 c1 0 88 20 d0 2a f0 0 f0 14 40 40 c8 5 c0 82 f0 0 f0 1e 40 40 d0 4 c9 f0 c1 0
  //   88 20 d0 28 40 40 d0 0 c9 84 c1 0 88 21 d9 1 88 20 c8 3 c0 f8 d9 1 88 21 d9 1 88 20 c9 87 c1 fc d0 0
  //   88 21 d9 1 88 20 d9 1 c8 80 c0 0 88 21 d9 1 88 20 40 32 40 2b 40 40 ff 0 0 0 ff ff 0 ff ff ff 0 ff
  //   5*0 ff 0 ff ff ff 0 ff 0 ff ff ff 0 7*ff 4*0 ff ff 0 ff ff ff 0 ff 4*0 ff ff 0 ff ff ff 0 ff 4*0
  //   9*ff 0 0 0 ff ff 0 ff ff ff 0 ff 0 5*ff 0 ff ff ff 0 ff ff 0 0 0 8*ff 4*0 ff ff 0 ff ff ff 0 ff 0 ff
  //   ff ff 0 ff 0 ff ff ff 0 ff 4*0 8*ff 5*0 ff 0 5*ff 4*0 ff ff 0 5*ff 5*0 7*ff 5*0 ff 0 5*ff 5*0 ff 0
  //   5*ff 0 11*ff 5*0 ff 0 5*ff 0 ff 0 0 0 ff 0 ff ff ff 0 ff 5*0 7*ff 0 ff ff ff 0 ff 0 ff ff ff 0 ff
  //   5*0 ff 0 ff ff ff 0 ff 0 ff ff ff 0 7*ff 5*0 ff ff ff 0 5*ff 0 5*ff 0 ff ff ff 5*0 7*ff 5*0 ff ff ff
  //   0 5*ff 0 ff ff ff 0 ff 0 4*ff 0 0 9*ff 0 ff ff 0 0 ff 0 ff 0 0 ff ff 0 0 0 ff ff ff 0 ff 0 0 ff ff 0
  //   ff ff 0 0 7*ff 0 5*ff 0 5*ff 0 5*ff 0 5*ff 5*0 7*ff 0 ff ff ff 0 ff 0 0 ff 0 0 ff 0 ff 0 ff 0 ff 0
  //   ff ff ff 0 ff 0 ff ff ff 0 7*ff 0 ff ff ff 0 ff 0 0 ff ff 0 ff 0 ff 0 ff 0 ff 0 ff ff 0 0 ff 0 ff ff
  //   ff 0 8*ff 0 0 0 ff ff 0 ff ff ff 0 ff 0 ff ff ff 0 ff 0 ff ff ff 0 ff ff 0 0 0 8*ff 4*0 ff ff 0 ff
  //   ff ff 0 ff 4*0 ff ff 0 5*ff 0 12*ff 0 0 0 ff ff 0 ff ff ff 0 ff 0 ff ff ff 0 ff 0 ff ff 0 ff ff ff 0
  //   0 ff 0 7*ff 4*0 ff ff 0 ff ff ff 0 ff 4*0 ff ff 0 ff 0 ff ff ff 0 ff ff 0 9*ff 4*0 ff 0 6*ff 0 0 0
  //   6*ff 0 ff ff 0 0 0 8*ff 5*0 ff ff ff 0 5*ff 0 5*ff 0 5*ff 0 9*ff 0 ff ff ff 0 ff 0 ff ff ff 0 ff 0
  //   ff ff ff 0 ff 0 ff ff ff 0 ff ff 0 0 0 8*ff 0 ff ff ff 0 ff 0 ff ff ff 0 ff ff 0 ff 0 ff ff ff 0 ff
  //   0 4*ff 0 9*ff 0 ff ff ff 0 ff 0 ff 0 ff 0 ff 0 ff 0 ff 0 ff 0 ff 0 ff 0 ff ff 0 ff 0 8*ff 0 ff ff ff
  //   0 ff ff 0 ff 0 4*ff 0 4*ff 0 ff 0 ff ff 0 ff ff ff 0 7*ff 0 7*ff 0 5*ff 0 ff ff ff 0 9*ff 0 11*ff 0
  //   11*ff 0 19*ff 5*0 4*ff 0 4*ff 0 4*ff 0 4*ff 5*0 7*ff d2 0 4a 1 82 98 49 0 d0 0 cb 4 c3 50 43 41 e1 1
  //   90 98 cb 4 c3 50 43 41 cb 4 c3 4a 90 99 e1 1 43 43 41 32 41 2b 41 40 8d 98 cc f0 c4 1 a3 21 dc 1 a3
  //   20 43 21 43 20 d3 0 4b 1 a9 98 49 0 dc 1 83 32 a3 20 e1 1 d8 1 cb 4 c3 70 43 43 e2 1 43 32 43 2b db
  //   40 e4 2 a3 21 dc 1 a3 20 43 21 43 20 4a 0 cb 4 c3 6a 43 43 40 32 40 2b 40 32 40 2b 40 40 41 21 41 20
  //   e0 41 81 98 d0 24 ca 4 c2 2c f0 4 f0 b8 42 40 d1 60 88 99 d1 6 d2 6 43 32 43 2b cc 4 c4 56 f0 4 f0
  //   ce 44 40 40 32 40 2b 40 40 85 98 8c 98 45 21 45 20 44 21 44 20 d0 0 a8 32 40 21 40 20 d1 0 49 1 48 0
  //   c9 5 c1 20 41 41 a1 98 ca 4 c2 a4 f0 5 f0 0 42 40 40 32 40 2b 44 32 44 2b dc 6 cd f0 c5 1 ac 21 dd 1
  //   ac 20 45 32 45 2b dd 1 c9 4 c1 d8 41 40 e6 6 40 32 40 2b 40 40 40 21 40 20 41 21 41 20 42 21 42 20
  //   43 21 43 20 44 21 44 20 45 21 45 20 0 3 c8 88 c0 0 81 2b d8 1 81 32 d9 1 e0 1 81 21 d8 1 81 20 d9 40
  //   88 98 d1 0 cd 4 c5 a4 f0 5 f0 66 45 40 0 4 45 32 45 2b 44 32 44 2b 43 32 43 2b 42 32 42 2b 41 32 41
  //   2b 40 32 40 2b 0 2 c8 88 c0 0 d1 0 81 21 d8 1 81 20 c8 f0 c0 d c9 5 c1 28 81 21 d8 1 81 20 c8 f0 c0
  //   f d1 3 81 20 c8 5 c0 a8 40 40 d0 26 40 40
endmodule

module ram_chip (
  input  [14:0] address,
  input  write_disable,
  input  [7:0] write_value,
  input  output_disable,
  output [7:0] read_value
);

  wire not_1_out;
  wire [7:0] ram_1_dout;

  RAM #(.addrWidth(15), .trigger("high")) ram_1 (
    .addr(address), .we(not_1_out), .oe(1'b1), .din(write_value), .dout(ram_1_dout));
  not not_1 (not_1_out, write_disable);
  tri_state_switch_8 tri_state_switch_8_1 (.a(ram_1_dout), .disable_output(output_disable), .out_3(read_value));
endmodule

module comparison_mux (
  input  [15:0] in_1,
  input  [15:0] in_2,
  input  [15:0] in_3,
  input  [15:0] in_4,
  input  [15:0] in_5,
  input  [15:0] in_6,
  input  [15:0] in_7,
  input  [15:0] in_8,
  input  [2:0] comp_select,
  output [15:0] out_10
);

  wire [15:0] mux_16_1_o, mux_16_2_o, mux_16_3_o, mux_16_4_o, mux_16_5_o, mux_16_6_o;

  mux_16 mux_16_1 (.a(in_1), .b(in_2), .ab(comp_select[0]), .o(mux_16_1_o));
  mux_16 mux_16_2 (.a(in_3), .b(in_4), .ab(comp_select[0]), .o(mux_16_2_o));
  mux_16 mux_16_3 (.a(in_5), .b(in_6), .ab(comp_select[0]), .o(mux_16_3_o));
  mux_16 mux_16_4 (.a(in_7), .b(in_8), .ab(comp_select[0]), .o(mux_16_4_o));
  mux_16 mux_16_5 (.a(mux_16_1_o), .b(mux_16_2_o), .ab(comp_select[1]), .o(mux_16_5_o));
  mux_16 mux_16_6 (.a(mux_16_3_o), .b(mux_16_4_o), .ab(comp_select[1]), .o(mux_16_6_o));
  mux_16 mux_16_7 (.a(mux_16_5_o), .b(mux_16_6_o), .ab(comp_select[2]), .o(out_10));
endmodule

module program_counter (
  input  count_enable,
  input  [15:0] jump_addr,
  input  clock,
  input  disable_jump,
  output [15:0] accum
);

  wire n74163_1_pin1, n74163_1_pin10, n74163_2_pin10, n74163_3_pin10;

  _74163 u_74163_1 (
    .pin1(n74163_1_pin1), .pin2(clock), .pin3(jump_addr[12]), .pin4(jump_addr[13]), .pin5(jump_addr[14]),
    .pin6(jump_addr[15]), .pin7(n74163_1_pin1), .pin14(accum[12]), .pin13(accum[13]), .pin12(accum[14]),
    .pin11(accum[15]), .pin10(n74163_1_pin10), .pin9(disable_jump));  // open: pin15
  _74163 u_74163_2 (
    .pin1(n74163_1_pin1), .pin2(clock), .pin3(jump_addr[8]), .pin4(jump_addr[9]), .pin5(jump_addr[10]),
    .pin6(jump_addr[11]), .pin7(n74163_1_pin1), .pin15(n74163_1_pin10), .pin14(accum[8]), .pin13(accum[9]),
    .pin12(accum[10]), .pin11(accum[11]), .pin10(n74163_2_pin10), .pin9(disable_jump));
  _74163 u_74163_3 (
    .pin1(n74163_1_pin1), .pin2(clock), .pin3(jump_addr[4]), .pin4(jump_addr[5]), .pin5(jump_addr[6]),
    .pin6(jump_addr[7]), .pin7(n74163_1_pin1), .pin15(n74163_2_pin10), .pin14(accum[4]), .pin13(accum[5]),
    .pin12(accum[6]), .pin11(accum[7]), .pin10(n74163_3_pin10), .pin9(disable_jump));
  _74163 u_74163_4 (
    .pin1(n74163_1_pin1), .pin2(clock), .pin3(jump_addr[0]), .pin4(jump_addr[1]), .pin5(jump_addr[2]),
    .pin6(jump_addr[3]), .pin7(n74163_1_pin1), .pin15(n74163_3_pin10), .pin14(accum[0]), .pin13(accum[1]),
    .pin12(accum[2]), .pin11(accum[3]), .pin10(count_enable), .pin9(disable_jump));
  // also tied to VCC on the sheet: n74163_1_pin1
endmodule

module stack_constroller (
  input  clock,
  input  not_select_1,
  input  not_select_2,
  input  [15:0] write_value,
  input  disable_upper,
  input  disable_lower,
  input  push,
  input  pop,
  input  [7:0] push_value,
  input  [7:0] ram_read,
  output [15:0] read_1,
  output [15:0] read_2,
  output [15:0] value,
  output not_ram_write,
  output [7:0] ram_value,
  output [15:0] ram_addr,
  output [7:0] pop_value
);

  wire n7432_1_pin3, n7432_1_pin6, n7432_1_pin8, not_1_out, not_3_out;

  _7432 u_7432_1 (
    .pin1(clock), .pin2(disable_lower), .pin3(n7432_1_pin3), .pin4(clock), .pin5(disable_upper),
    .pin6(n7432_1_pin6), .pin10(pop), .pin9(push), .pin8(n7432_1_pin8));  // open: pin13, pin12, pin11
  not not_1 (not_1_out, pop);
  not not_2 (not_ram_write, push);
  not not_3 (not_3_out, n7432_1_pin8);
  up_down_counter_16 up_down_counter_16_1 (
    .disable_lower(n7432_1_pin3), .disable_upper(n7432_1_pin6), .count_in(write_value),
    .not_count_down(not_1_out), .not_count_up(not_ram_write), .count_out(value));  // open: not_carry_out, not_borrow_out
  tri_state_switch_8 tri_state_switch_8_1 (.a(push_value), .disable_output(not_ram_write), .out_3(ram_value));
  tri_state_switch_16 tri_state_switch_16_1 (.a(value), .disable_output(not_select_1), .out_3(read_1));
  tri_state_switch_16 tri_state_switch_16_2 (.a(value), .disable_output(not_select_2), .out_3(read_2));
  tri_state_switch_16 tri_state_switch_16_3 (.a(value), .disable_output(not_3_out), .out_3(ram_addr));

  assign pop_value = ram_read;

  // Notes on the sheet:
  //   disable_upper: initial=0x1
  //   disable_lower: initial=0x1
endmodule

module opcode_decoder (
  input  [7:0] read_inst,
  input  inst_complete,
  input  clock,
  output [15:0] instruction,
  output not_read_program
);

  wire n7402_1_pin2, n7402_1_pin4, n7402_1_pin10, n7402_1_pin11, n7402_1_pin13, n7474_1_pin2, n7474_1_pin5;

  _7402 u_7402_1 (
    .pin1(not_read_program), .pin2(n7402_1_pin2), .pin3(n7402_1_pin2), .pin4(n7402_1_pin4),
    .pin5(inst_complete), .pin6(inst_complete), .pin13(n7402_1_pin13), .pin12(n7402_1_pin2),
    .pin11(n7402_1_pin11), .pin10(n7402_1_pin10), .pin9(n7402_1_pin13), .pin8(n7402_1_pin13));
  _7474 u_7474_1 (
    .pin1(n7402_1_pin4), .pin2(n7474_1_pin2), .pin3(clock), .pin5(n7474_1_pin5), .pin6(n7402_1_pin11),
    .pin13(n7402_1_pin4), .pin12(n7474_1_pin5), .pin11(clock), .pin9(n7402_1_pin2));  // open: pin4, pin10, pin8
  register_8 opcode_register_lower (.data(read_inst), .clken(n7474_1_pin5), .clk(clock), .out_4(instruction[15:8]));
  register_8 opcode_register_upper (.data(read_inst), .clken(n7402_1_pin10), .clk(clock), .out_4(instruction[7:0]));
  // also tied to VCC on the sheet: n7474_1_pin2
endmodule

module bus_encoder (
  input  [15:0] instruction,
  input  execute_disable,
  output [7:0] destination_register,
  output [7:0] source_register,
  output [15:0] value_1,
  output [15:0] value_2,
  output [15:0] write_value,
  output [2:0] instruction_stage,
  output jump,
  output write_lower,
  output write_upper,
  output write_mem,
  output read_mem,
  output stack,
  output compare,
  output logical,
  output compare_set,
  output flip_mem,
  output memory,
  output simple,
  output [7:0] operation_select,
  output [2:0] destination_select
);

  wire n7400_1_pin2, n7400_1_pin3, n7400_1_pin8, n7400_2_pin3, n7408_1_pin3, n7408_1_pin6, n7408_1_pin8,
       n7408_1_pin10, n7408_1_pin11, n7408_1_pin12, n7408_1_pin13, n7408_2_pin8, n7408_3_pin2, n7408_3_pin6,
       n7408_3_pin9, n7408_3_pin12, n7414_1_pin2, n7414_1_pin4, n7414_1_pin6, n7414_1_pin8, n7414_1_pin10,
       n7414_1_pin12, n7432_1_pin2, n7432_1_pin3, n7432_1_pin5, n7432_1_pin6, n7432_1_pin10, n7432_1_pin12,
       n7432_2_pin2, n7432_2_pin8, n7432_2_pin11, n7432_3_pin6, n7432_3_pin8, n7436_1_pin1, n7436_1_pin3,
       n7436_1_pin6;
  wire [2:0] bit_extender_1_out, n7400_2_pin11;
  wire [3:0] mux_4_1_out_4;
  wire [3:3] undriven;
  wire [7:0] n7408_3_pin11, switched_decoder_3_3_decoded;
  wire [7:1] bit_decoder_3_1_decoded;

  assign bit_extender_1_out = {{1{1'b0}}, instruction[15:14]};  // Bit_Extender bit_extender_1
  bit_decoder_3 bit_decoder_3_1 (.in_1(bit_extender_1_out), .decoded({bit_decoder_3_1_decoded, n7408_3_pin11[7]}));
  _7414 u_7414_1 (
    .pin1(instruction[6]), .pin2(n7414_1_pin2), .pin3(instruction[7]), .pin4(n7414_1_pin4),
    .pin5(instruction[11]), .pin6(n7414_1_pin6), .pin13(instruction[5]), .pin12(n7414_1_pin12),
    .pin11(instruction[4]), .pin10(n7414_1_pin10), .pin9(instruction[3]), .pin8(n7414_1_pin8));
  switched_decoder_3 switched_decoder_3_1 (
    .in_1(instruction[10:8]), .output_disable(n7432_2_pin8), .decoded(destination_register));
  switched_decoder_3 switched_decoder_3_2 (
    .in_1(instruction[13:11]), .output_disable(n7436_1_pin6), .decoded(source_register));
  _7432 u_7432_1 (
    .pin1(execute_disable), .pin2(n7432_1_pin2), .pin3(n7432_1_pin3), .pin4(execute_disable),
    .pin5(n7432_1_pin5), .pin6(n7432_1_pin6), .pin13(switched_decoder_3_3_decoded[1]), .pin12(n7432_1_pin12),
    .pin11(n7432_1_pin5), .pin10(n7432_1_pin10), .pin9(n7432_1_pin12), .pin8(n7432_1_pin2));
  _7432 u_7432_2 (
    .pin1(bit_decoder_3_1_decoded[3]), .pin2(n7432_2_pin2), .pin3(n7432_1_pin12), .pin13(execute_disable),
    .pin12(switched_decoder_3_3_decoded[2]), .pin11(n7432_2_pin11), .pin10(execute_disable),
    .pin9(n7432_2_pin2), .pin8(n7432_2_pin8));  // open: pin4, pin5, pin6
  _7400 u_7400_1 (
    .pin1(switched_decoder_3_3_decoded[5]), .pin2(n7400_1_pin2), .pin3(n7400_1_pin3), .pin4(n7400_1_pin3),
    .pin5(n7400_1_pin3), .pin6(n7408_3_pin11[6]), .pin13(switched_decoder_3_3_decoded[1]),
    .pin12(switched_decoder_3_3_decoded[1]), .pin11(n7432_1_pin10), .pin10(n7432_1_pin12),
    .pin9(n7432_1_pin12), .pin8(n7400_1_pin8));
  tri_state_switch_8 tri_state_switch_8_1 (.a({8{1'b0}}), .disable_output(n7432_2_pin11), .out_3(value_2[15:8]));
  switched_decoder_3 switched_decoder_3_3 (
    .in_1(instruction[13:11]), .output_disable(bit_decoder_3_1_decoded[3]),
    .decoded(switched_decoder_3_3_decoded));
  tri_state_switch_8 tri_state_switch_8_2 (
    .a(instruction[7:0]), .disable_output(switched_decoder_3_3_decoded[6]), .out_3(value_1[7:0]));
  tri_state_switch_8 tri_state_switch_8_3 (.a(instruction[7:0]), .disable_output(n7432_1_pin3), .out_3(value_2[7:0]));
  tri_state_switch_8 tri_state_switch_8_4 (.a(instruction[7:0]), .disable_output(n7432_1_pin6), .out_3(value_2[15:8]));
  _7432 u_7432_3 (
    .pin1(n7414_1_pin12), .pin2(bit_decoder_3_1_decoded[2]), .pin3(n7400_1_pin2), .pin4(n7414_1_pin12),
    .pin5(bit_decoder_3_1_decoded[1]), .pin6(n7432_3_pin6), .pin13(bit_decoder_3_1_decoded[1]),
    .pin12(n7414_1_pin6), .pin11(n7408_3_pin11[5]), .pin10(n7400_1_pin8), .pin9(execute_disable),
    .pin8(n7432_3_pin8));
  _7408 u_7408_1 (
    .pin1(switched_decoder_3_3_decoded[1]), .pin2(switched_decoder_3_3_decoded[2]), .pin3(n7408_1_pin3),
    .pin4(n7408_1_pin3), .pin5(switched_decoder_3_3_decoded[0]), .pin6(n7408_1_pin6), .pin13(n7408_1_pin13),
    .pin12(n7408_1_pin12), .pin11(n7408_1_pin11), .pin10(n7408_1_pin10), .pin9(n7408_1_pin12),
    .pin8(n7408_1_pin8));
  _7408 u_7408_2 (
    .pin1(switched_decoder_3_3_decoded[1]), .pin2(switched_decoder_3_3_decoded[2]), .pin3(n7408_1_pin10),
    .pin4(n7432_3_pin6), .pin5(switched_decoder_3_3_decoded[6]), .pin6(n7408_3_pin11[2]),
    .pin13(switched_decoder_3_3_decoded[2]), .pin12(switched_decoder_3_3_decoded[0]), .pin11(n7408_1_pin13),
    .pin10(n7408_1_pin6), .pin9(n7408_1_pin12), .pin8(n7408_2_pin8));
  _7436 u_7436_1 (
    .pin1(n7436_1_pin1), .pin2(n7432_3_pin8), .pin3(n7436_1_pin3), .pin4(n7436_1_pin3), .pin5(n7436_1_pin3),
    .pin6(n7436_1_pin6), .pin13(n7408_3_pin11[2]), .pin12(n7408_3_pin11[2]), .pin11(n7436_1_pin1),
    .pin10(switched_decoder_3_3_decoded[6]), .pin9(switched_decoder_3_3_decoded[6]), .pin8(n7432_2_pin2));
  _7400 u_7400_2 (
    .pin1(switched_decoder_3_3_decoded[3]), .pin2(switched_decoder_3_3_decoded[4]), .pin3(n7400_2_pin3),
    .pin4(n7400_2_pin3), .pin5(n7400_2_pin3), .pin6(n7408_1_pin12), .pin13(switched_decoder_3_3_decoded[3]),
    .pin12(switched_decoder_3_3_decoded[3]), .pin11(n7400_2_pin11[0]),
    .pin10(switched_decoder_3_3_decoded[4]), .pin9(switched_decoder_3_3_decoded[4]), .pin8(n7400_2_pin11[1]));
  _7408 u_7408_3 (
    .pin1(n7408_2_pin8), .pin2(n7408_3_pin2), .pin3(n7408_3_pin11[4]), .pin4(bit_decoder_3_1_decoded[2]),
    .pin5(bit_decoder_3_1_decoded[1]), .pin6(n7408_3_pin6), .pin13(n7408_1_pin11), .pin12(n7408_3_pin12),
    .pin11(n7408_3_pin11[0]), .pin10(n7408_1_pin8), .pin9(n7408_3_pin9), .pin8(n7408_3_pin11[1]));
  _7432 u_7432_4 (
    .pin1(n7408_3_pin6), .pin2(n7414_1_pin4), .pin3(n7408_3_pin2), .pin4(bit_decoder_3_1_decoded[1]),
    .pin5(n7414_1_pin2), .pin6(n7408_3_pin11[3]), .pin13(n7408_3_pin6), .pin12(n7414_1_pin10),
    .pin11(n7408_3_pin12), .pin10(n7408_3_pin6), .pin9(n7414_1_pin8), .pin8(n7408_3_pin9));
  mux_4 mux_4_1 (
    .a({undriven[3], n7400_2_pin11}), .b(instruction[3:0]), .ab(bit_decoder_3_1_decoded[3]),
    .out_4(mux_4_1_out_4));
  bit_decoder_3 bit_decoder_3_2 (.in_1(mux_4_1_out_4[2:0]), .decoded(operation_select));
  tri_state_switch_8 tri_state_switch_8_5 (
    .a(n7408_3_pin11), .disable_output(execute_disable),
    .out_3({simple, memory, compare_set, logical, compare, stack, write_upper, write_lower}));
  // NoConnect on write_value
  // NoConnect on instruction_stage
  // NoConnect on jump
  // NoConnect on write_mem
  // NoConnect on read_mem
  // NoConnect on flip_mem

  assign destination_select = instruction[10:8];

  // Notes on the sheet:
  //   H
  //   a
  //   b
  //   G
  //   E
  //   F
  //   J
  //   D
  //   K
  //   or this with immediate controll other one
  //   L
  //   M
  //   Mode 3 Upper
  //   Mode 3 Lower
  //   C
  //   I
endmodule

module main_register (
  input  clock,
  input  not_select_1,
  input  not_select_2,
  input  [15:0] write_value,
  input  disable_upper,
  input  disable_lower,
  output [15:0] read_1,
  output [15:0] read_2,
  output [15:0] value
);

  wire n7432_1_pin3, n7432_1_pin6;

  _7432 u_7432_1 (
    .pin1(not_select_1), .pin2(disable_upper), .pin3(n7432_1_pin3), .pin4(not_select_1),
    .pin5(disable_lower), .pin6(n7432_1_pin6));  // open: pin13, pin12, pin11, pin10, pin9, pin8
  register_8 register_8_1 (.data(write_value[7:0]), .clken(n7432_1_pin6), .clk(clock), .out_4(value[7:0]));
  register_8 register_8_2 (.data(write_value[15:8]), .clken(n7432_1_pin3), .clk(clock), .out_4(value[15:8]));
  tri_state_switch_16 tri_state_switch_16_1 (.a(value), .disable_output(not_select_1), .out_3(read_1));
  tri_state_switch_16 tri_state_switch_16_2 (.a(value), .disable_output(not_select_2), .out_3(read_2));
endmodule

module immediate_controller (
  input  [3:0] opcode_format,
  input  [7:0] opcode_lower,
  output [15:0] value_2
);

  wire [15:0] bit_extender_1_out;

  assign bit_extender_1_out = {{8{1'b0}}, opcode_lower};  // Bit_Extender bit_extender_1
  tri_state_switch_16 tri_state_switch_16_1 (
    .a(bit_extender_1_out), .disable_output(opcode_format[3]), .out_3(value_2));
endmodule

module register_value_controller (
  input  [3:0] opcode_format,
  input  [15:0] register_value_1,
  input  [15:0] register_value_2,
  output [15:0] value_1,
  output [15:0] value_2
);

  wire n7408_1_pin11;

  _7408 u_7408_1 (
    .pin13(opcode_format[1]), .pin12(opcode_format[2]), .pin11(n7408_1_pin11));  // open: pin1, pin2, pin3, pin4, pin5, pin6, pin10, pin9, pin8
  tri_state_switch_16 tri_state_switch_16_1 (.a(register_value_1), .disable_output(n7408_1_pin11), .out_3(value_1));
  tri_state_switch_16 tri_state_switch_16_2 (.a(register_value_2), .disable_output(opcode_format[2]), .out_3(value_2));
endmodule

module microcode_decoder (
  input  [3:0] opcode_format
);
endmodule

module mode_3_controller (
  input  [3:0] opcode_format,
  input  [7:0] opcode_upper,
  input  [15:0] value_2,
  output [15:0] write_value,
  output disable_lower,
  output disable_upper
);

  wire n7408_1_pin3, n7408_1_pin6, n7408_1_pin8, n7408_1_pin11;
  wire [7:0] bit_decoder_3_1_decoded, tri_state_switch_8_1_out_3, tri_state_switch_8_2_out_3;
  wire [15:0] tri_state_switch_16_1_out_3;

  bit_decoder_3 bit_decoder_3_1 (.in_1(opcode_upper[5:3]), .decoded(bit_decoder_3_1_decoded));
  _7408 u_7408_1 (
    .pin1(bit_decoder_3_1_decoded[2]), .pin2(bit_decoder_3_1_decoded[1]), .pin3(n7408_1_pin3),
    .pin4(n7408_1_pin3), .pin5(bit_decoder_3_1_decoded[0]), .pin6(n7408_1_pin6),
    .pin13(bit_decoder_3_1_decoded[1]), .pin12(bit_decoder_3_1_decoded[2]), .pin11(n7408_1_pin11),
    .pin10(bit_decoder_3_1_decoded[0]), .pin9(bit_decoder_3_1_decoded[2]), .pin8(n7408_1_pin8));
  tri_state_switch_8 tri_state_switch_8_1 (
    .a(value_2[7:0]), .disable_output(n7408_1_pin8), .out_3(tri_state_switch_8_1_out_3));
  tri_state_switch_8 tri_state_switch_8_2 (
    .a(value_2[7:0]), .disable_output(bit_decoder_3_1_decoded[1]), .out_3(tri_state_switch_8_2_out_3));
  tri_state_switch_8 tri_state_switch_8_3 (
    .a({8{1'b0}}), .disable_output(bit_decoder_3_1_decoded[2]), .out_3(tri_state_switch_8_2_out_3));
  tri_state_switch_16 tri_state_switch_16_1 (
    .a({tri_state_switch_8_2_out_3, tri_state_switch_8_1_out_3}), .disable_output(n7408_1_pin6),
    .out_3(tri_state_switch_16_1_out_3));
  _7432 u_7432_1 (
    .pin13(opcode_format[3]), .pin12(n7408_1_pin8), .pin11(disable_lower), .pin10(opcode_format[3]),
    .pin9(n7408_1_pin11), .pin8(disable_upper));  // open: pin1, pin2, pin3, pin4, pin5, pin6
  tri_state_switch_16 tri_state_switch_16_2 (
    .a(tri_state_switch_16_1_out_3), .disable_output(opcode_format[3]), .out_3(write_value));
endmodule

module mode_2_controller (
  input  [3:0] opcode_format,
  input  [15:0] value_1,
  input  [15:0] value_2,
  input  [7:0] opcode_lower,
  output [15:0] write_value,
  output disable_lower,
  output disable_upper
);

  wire n7421_1_pin5, n7421_1_pin6, n7421_1_pin8;
  wire [15:0] alu_1_o, and_16_1_out_3, bit_decoder_4_1_out_2, or_16_1_out_3, tri_state_switch_16_1_out_3,
       xor_16_1_out_3;

  bit_decoder_4 bit_decoder_4_1 (.in_1(opcode_lower[3:0]), .out_2(bit_decoder_4_1_out_2));
  tri_state_switch_16 tri_state_switch_16_1 (
    .a(value_2), .disable_output(bit_decoder_4_1_out_2[0]), .out_3(tri_state_switch_16_1_out_3));
  alu alu_1 (.a(value_1), .b(value_2), .negate_b(bit_decoder_4_1_out_2[1]), .o(alu_1_o));  // open: cin, cout
  and_16 and_16_1 (.a(value_1), .b(value_2), .out_3(and_16_1_out_3));
  or_16 or_16_1 (.a(value_1), .b(value_2), .out_3(or_16_1_out_3));
  xor_16 xor_16_1 (.a(value_1), .b(value_2), .out_3(xor_16_1_out_3));
  tri_state_switch_16 tri_state_switch_16_2 (
    .a(alu_1_o), .disable_output(bit_decoder_4_1_out_2[1]), .out_3(tri_state_switch_16_1_out_3));
  tri_state_switch_16 tri_state_switch_16_3 (
    .a(alu_1_o), .disable_output(bit_decoder_4_1_out_2[2]), .out_3(tri_state_switch_16_1_out_3));
  tri_state_switch_16 tri_state_switch_16_4 (
    .a(and_16_1_out_3), .disable_output(bit_decoder_4_1_out_2[3]), .out_3(tri_state_switch_16_1_out_3));
  tri_state_switch_16 tri_state_switch_16_5 (
    .a(or_16_1_out_3), .disable_output(bit_decoder_4_1_out_2[4]), .out_3(tri_state_switch_16_1_out_3));
  tri_state_switch_16 tri_state_switch_16_6 (
    .a(xor_16_1_out_3), .disable_output(bit_decoder_4_1_out_2[5]), .out_3(tri_state_switch_16_1_out_3));
  _7421 u_7421_1 (
    .pin1(bit_decoder_4_1_out_2[3]), .pin2(bit_decoder_4_1_out_2[4]), .pin4(bit_decoder_4_1_out_2[5]),
    .pin5(n7421_1_pin5), .pin6(n7421_1_pin6), .pin13(n7421_1_pin6), .pin12(bit_decoder_4_1_out_2[2]),
    .pin10(bit_decoder_4_1_out_2[1]), .pin9(bit_decoder_4_1_out_2[0]), .pin8(n7421_1_pin8));  // open: pin3, pin11
  _7432 u_7432_1 (
    .pin10(n7421_1_pin8), .pin9(opcode_format[2]), .pin8(disable_lower));  // open: pin1, pin2, pin3, pin4, pin5, pin6, pin13, pin12, pin11
  tri_state_switch_16 tri_state_switch_16_7 (
    .a(tri_state_switch_16_1_out_3), .disable_output(opcode_format[2]), .out_3(write_value));

  assign disable_upper = disable_lower;
  // also tied to VCC on the sheet: n7421_1_pin5
endmodule

module mode_1_controller (
  input  [3:0] opcode_format,
  input  [15:0] value_1,
  input  [15:0] value_2,
  input  [7:0] opcode_lower,
  output [15:0] write_value,
  output disable_lower,
  output disable_upper,
  output [15:0] jump_addr,
  output disable_jump
);

  wire [15:0] bit_decoder_4_1_out_2, undriven;

  bit_decoder_4 bit_decoder_4_1 (.in_1(opcode_lower[3:0]), .out_2(bit_decoder_4_1_out_2));
  _7432 u_7432_1 (
    .pin13(bit_decoder_4_1_out_2[4]), .pin12(opcode_format[1]), .pin11(disable_jump));  // open: pin1, pin2, pin3, pin4, pin5, pin6, pin10, pin9, pin8
  tri_state_switch_16 tri_state_switch_16_1 (.a(undriven), .disable_output(opcode_format[1]), .out_3(write_value));
  tri_state_switch_16 tri_state_switch_16_2 (.a(value_1), .disable_output(disable_jump), .out_3(jump_addr));

  assign disable_lower = 1'b1;
  assign disable_upper = 1'b1;
endmodule

module alu (
  input  [15:0] a,
  input  [15:0] b,
  input  negate_b,
  input  cin,
  output [15:0] o,
  output cout
);

  wire [15:0] mux_16_1_o, negate_16_1_inverted;

  negate_16 negate_16_1 (.invert(b), .inverted(negate_16_1_inverted));
  mux_16 mux_16_1 (.a(b), .b(negate_16_1_inverted), .ab(negate_b), .o(mux_16_1_o));
  adder_16 adder_16_1 (.a(a), .b(mux_16_1_o), .cin(cin), .sum(o), .cout(cout));
endmodule

module up_down_counter_16 (
  input  disable_lower,
  input  disable_upper,
  input  [15:0] count_in,
  input  not_count_down,
  input  not_count_up,
  output not_carry_out,
  output not_borrow_out,
  output [15:0] count_out
);

  wire n74193_1_pin4, n74193_1_pin5, n74193_1_pin14, n74193_2_pin4, n74193_2_pin5, n74193_3_pin4,
       n74193_3_pin5;

  _74193 u_74193_1 (
    .pin1(count_in[13]), .pin2(count_out[13]), .pin3(count_out[12]), .pin4(n74193_1_pin4),
    .pin5(n74193_1_pin5), .pin6(count_out[14]), .pin7(count_out[15]), .pin15(count_in[12]),
    .pin14(n74193_1_pin14), .pin13(not_borrow_out), .pin12(not_carry_out), .pin11(disable_upper),
    .pin10(count_in[14]), .pin9(count_in[15]));
  _74193 u_74193_2 (
    .pin1(count_in[9]), .pin2(count_out[9]), .pin3(count_out[8]), .pin4(n74193_2_pin4), .pin5(n74193_2_pin5),
    .pin6(count_out[10]), .pin7(count_out[11]), .pin15(count_in[8]), .pin14(n74193_1_pin14),
    .pin13(n74193_1_pin4), .pin12(n74193_1_pin5), .pin11(disable_upper), .pin10(count_in[10]),
    .pin9(count_in[11]));
  _74193 u_74193_3 (
    .pin1(count_in[5]), .pin2(count_out[5]), .pin3(count_out[4]), .pin4(n74193_3_pin4), .pin5(n74193_3_pin5),
    .pin6(count_out[6]), .pin7(count_out[7]), .pin15(count_in[4]), .pin14(n74193_1_pin14),
    .pin13(n74193_2_pin4), .pin12(n74193_2_pin5), .pin11(disable_lower), .pin10(count_in[6]),
    .pin9(count_in[7]));
  _74193 u_74193_4 (
    .pin1(count_in[1]), .pin2(count_out[1]), .pin3(count_out[0]), .pin4(not_count_down), .pin5(not_count_up),
    .pin6(count_out[2]), .pin7(count_out[3]), .pin15(count_in[0]), .pin14(n74193_1_pin14),
    .pin13(n74193_3_pin4), .pin12(n74193_3_pin5), .pin11(disable_lower), .pin10(count_in[2]),
    .pin9(count_in[3]));
  // also tied to GND on the sheet: n74193_1_pin14

  // Notes on the sheet:
  //   not_count_down: initial=0x1
  //   not_count_up: initial=0x1
endmodule

module adder_16 (
  input  [15:0] a,
  input  [15:0] b,
  input  cin,
  output [15:0] sum,
  output cout
);

  wire adder_8_1_cout;

  adder_8 adder_8_1 (.a(a[7:0]), .b(b[7:0]), .cin(cin), .sum(sum[7:0]), .cout(adder_8_1_cout));
  adder_8 adder_8_2 (.a(a[15:8]), .b(b[15:8]), .cin(adder_8_1_cout), .sum(sum[15:8]), .cout(cout));
endmodule

module adder_8 (
  input  [7:0] a,
  input  [7:0] b,
  input  cin,
  output [7:0] sum,
  output cout
);

  wire n74283_1_pin7;

  _74283 u_74283_1 (
    .pin1(sum[5]), .pin2(b[5]), .pin3(a[5]), .pin4(sum[4]), .pin5(a[4]), .pin6(b[4]), .pin7(n74283_1_pin7),
    .pin15(b[6]), .pin14(a[6]), .pin13(sum[6]), .pin12(a[7]), .pin11(b[7]), .pin10(sum[7]), .pin9(cout));
  _74283 u_74283_2 (
    .pin1(sum[1]), .pin2(b[1]), .pin3(a[1]), .pin4(sum[0]), .pin5(a[0]), .pin6(b[0]), .pin7(cin),
    .pin15(b[2]), .pin14(a[2]), .pin13(sum[2]), .pin12(a[3]), .pin11(b[3]), .pin10(sum[3]),
    .pin9(n74283_1_pin7));
endmodule

module negate_16 (
  input  [15:0] invert,
  output [15:0] inverted
);

  wire adder_16_1_cout;
  wire [15:0] n7414_1_pin12;

  _7414 u_7414_1 (
    .pin1(invert[5]), .pin2(n7414_1_pin12[5]), .pin3(invert[4]), .pin4(n7414_1_pin12[4]), .pin5(invert[3]),
    .pin6(n7414_1_pin12[3]), .pin13(invert[0]), .pin12(n7414_1_pin12[0]), .pin11(invert[1]),
    .pin10(n7414_1_pin12[1]), .pin9(invert[2]), .pin8(n7414_1_pin12[2]));
  _7414 u_7414_2 (
    .pin1(invert[11]), .pin2(n7414_1_pin12[11]), .pin3(invert[10]), .pin4(n7414_1_pin12[10]),
    .pin5(invert[9]), .pin6(n7414_1_pin12[9]), .pin13(invert[6]), .pin12(n7414_1_pin12[6]),
    .pin11(invert[7]), .pin10(n7414_1_pin12[7]), .pin9(invert[8]), .pin8(n7414_1_pin12[8]));
  _7414 u_7414_3 (
    .pin5(invert[15]), .pin6(n7414_1_pin12[15]), .pin13(invert[12]), .pin12(n7414_1_pin12[12]),
    .pin11(invert[13]), .pin10(n7414_1_pin12[13]), .pin9(invert[14]), .pin8(n7414_1_pin12[14]));  // open: pin1, pin2, pin3, pin4
  adder_16 adder_16_1 (.a({16{1'b0}}), .b(n7414_1_pin12), .cin(1'b1), .sum(inverted), .cout(adder_16_1_cout));
endmodule

module subber_4 (
  input  [3:0] a,
  input  cin,
  input  [3:0] b,
  output cout,
  output [3:0] sum
);

  wire n7414_1_pin10, n7414_1_pin11, n7414_1_pin12, n7414_1_pin13, n74283_1_pin2, n74283_1_pin6,
       n74283_1_pin11, n74283_1_pin15;

  _74283 u_74283_1 (
    .pin1(sum[1]), .pin2(n74283_1_pin2), .pin3(a[1]), .pin4(sum[0]), .pin5(a[0]), .pin6(n74283_1_pin6),
    .pin7(cin), .pin15(n74283_1_pin15), .pin14(a[2]), .pin13(sum[2]), .pin12(a[3]), .pin11(n74283_1_pin11),
    .pin10(sum[3]), .pin9(cout));
  _7414 u_7414_1 (
    .pin1(b[3]), .pin2(n74283_1_pin11), .pin3(b[2]), .pin4(n74283_1_pin15), .pin5(b[1]),
    .pin6(n74283_1_pin2), .pin13(n7414_1_pin13), .pin12(n7414_1_pin12), .pin11(n7414_1_pin11),
    .pin10(n7414_1_pin10), .pin9(b[0]), .pin8(n74283_1_pin6));
  Pull_Resistor pull_resistor_1 (.node(n7414_1_pin12));
  Pull_Resistor pull_resistor_2 (.node(n7414_1_pin10));
  Pull_Resistor #(.pull(1)) pull_resistor_3 (.node(n7414_1_pin13));
  Pull_Resistor #(.pull(1)) pull_resistor_4 (.node(n7414_1_pin11));
endmodule

module mux_4 (
  input  [3:0] a,
  input  [3:0] b,
  input  ab,
  output [3:0] out_4
);

  wire pull_resistor_1_node;

  Pull_Resistor pull_resistor_1 (.node(pull_resistor_1_node));
  // DIP_74157 dip_74157_1: pin names not known; wires that end beside it: out_4[2], b[2], a[2], out_4[3], b[3], a[3], pull_resistor_1_node, out_4[1], b[1], a[1], out_4[0], b[0], a[0], ab
endmodule

module mux_16 (
  input  [15:0] a,
  input  [15:0] b,
  input  ab,
  output [15:0] o
);

  mux_4 mux_4_1 (.a(a[3:0]), .b(b[3:0]), .ab(ab), .out_4(o[3:0]));
  mux_4 mux_4_2 (.a(a[7:4]), .b(b[7:4]), .ab(ab), .out_4(o[7:4]));
  mux_4 mux_4_3 (.a(a[11:8]), .b(b[11:8]), .ab(ab), .out_4(o[11:8]));
  mux_4 mux_4_4 (.a(a[15:12]), .b(b[15:12]), .ab(ab), .out_4(o[15:12]));
endmodule

module switch_4 (
  input  [3:0] a,
  input  switch,
  output [3:0] switched
);

  _74125 #(.ShowInternalStructure("true")) u_74125_1 (
    .pin1(switch), .pin2(a[2]), .pin3(switched[2]), .pin4(switch), .pin5(a[3]), .pin6(switched[3]),
    .pin13(switch), .pin12(a[1]), .pin11(switched[1]), .pin10(switch), .pin9(a[0]), .pin8(switched[0]));
endmodule

module switch_8 (
  input  [7:0] value,
  input  switch,
  output [7:0] out_3
);

  switch_4 switch_4_1 (.a(value[3:0]), .switch(switch), .switched(out_3[3:0]));
  switch_4 switch_4_2 (.a(value[7:4]), .switch(switch), .switched(out_3[7:4]));
endmodule

module switch_16 (
  input  [15:0] a,
  input  switch,
  output [15:0] switched
);

  switch_4 switch_4_1 (.a(a[3:0]), .switch(switch), .switched(switched[3:0]));
  switch_4 switch_4_2 (.a(a[7:4]), .switch(switch), .switched(switched[7:4]));
  switch_4 switch_4_3 (.a(a[11:8]), .switch(switch), .switched(switched[11:8]));
  switch_4 switch_4_4 (.a(a[15:12]), .switch(switch), .switched(switched[15:12]));
endmodule

module register_8 (
  input  [7:0] data,
  input  clken,
  input  clk,
  output [7:0] out_4
);

  _74377 #(.ShowInternalStructure("true")) u_74377_1 (
    .pin1(clken), .pin2(out_4[0]), .pin3(data[0]), .pin4(data[1]), .pin5(out_4[1]), .pin6(out_4[2]),
    .pin7(data[2]), .pin8(data[3]), .pin9(out_4[3]), .pin19(out_4[7]), .pin18(data[7]), .pin17(data[6]),
    .pin16(out_4[6]), .pin15(out_4[5]), .pin14(data[5]), .pin13(data[4]), .pin12(out_4[4]), .pin11(clk));
endmodule

module register_16 (
  input  [15:0] data,
  input  clken,
  input  clk,
  output [15:0] out_4
);

  register_8 register_8_1 (.data(data[7:0]), .clken(clken), .clk(clk), .out_4(out_4[7:0]));
  register_8 register_8_2 (.data(data[15:8]), .clken(clken), .clk(clk), .out_4(out_4[15:8]));
endmodule

module bit_decoder_3 (
  input  [2:0] in_1,
  output [7:0] decoded
);

  // DIP_74138 dip_74138_1: pin names not known; wires that end beside it: in_1[0], in_1[1], in_1[2], 1'b0, 1'b0, 1'b1, decoded[7], decoded[0], decoded[1], decoded[2], decoded[3], decoded[4], decoded[5], decoded[6]
endmodule

module bit_decoder_4 (
  input  [3:0] in_1,
  output [15:0] out_2
);

  // DIP_74138 dip_74138_1: pin names not known; wires that end beside it: in_1[0], in_1[1], in_1[2], in_1[3], 1'b0, out_2[0], out_2[1], out_2[2], out_2[3]
  // DIP_74138 dip_74138_2: pin names not known; wires that end beside it: 1'b1, out_2[7], in_1[0], in_1[1], in_1[2], 1'b0, 1'b0, in_1[3], out_2[15], out_2[4], out_2[5], out_2[6], out_2[8], out_2[9], out_2[10], out_2[11], out_2[12], out_2[13], out_2[14]
endmodule

module tri_state_switch_4 (
  input  [3:0] a,
  input  disable_output,
  output [3:0] o
);

  _74125 u_74125_1 (
    .pin1(disable_output), .pin2(a[2]), .pin3(o[2]), .pin4(disable_output), .pin5(a[3]), .pin6(o[3]),
    .pin13(disable_output), .pin12(a[1]), .pin11(o[1]), .pin10(disable_output), .pin9(a[0]), .pin8(o[0]));
endmodule

module tri_state_switch_8 (
  input  [7:0] a,
  input  disable_output,
  output [7:0] out_3
);

  _74244 #(.ShowInternalStructure("true")) u_74244_1 (
    .pin1(disable_output), .pin2(a[3]), .pin3(out_3[4]), .pin4(a[2]), .pin5(out_3[5]), .pin6(a[1]),
    .pin7(out_3[6]), .pin8(a[0]), .pin9(out_3[7]), .pin19(disable_output), .pin18(out_3[3]), .pin17(a[4]),
    .pin16(out_3[2]), .pin15(a[5]), .pin14(out_3[1]), .pin13(a[6]), .pin12(out_3[0]), .pin11(a[7]));
endmodule
module tri_state_switch_16 (
  input  [15:0] a,
  input  disable_output,
  output [15:0] out_3
);

  tri_state_switch_8 tri_state_switch_8_1 (.a(a[7:0]), .disable_output(disable_output), .out_3(out_3[7:0]));
  tri_state_switch_8 tri_state_switch_8_2 (.a(a[15:8]), .disable_output(disable_output), .out_3(out_3[15:8]));
endmodule

module and_16 (
  input  [15:0] a,
  input  [15:0] b,
  output [15:0] out_3
);

  _7408 u_7408_1 (
    .pin1(a[2]), .pin2(b[2]), .pin3(out_3[2]), .pin4(a[3]), .pin5(b[3]), .pin6(out_3[3]), .pin13(a[0]),
    .pin12(b[0]), .pin11(out_3[0]), .pin10(a[1]), .pin9(b[1]), .pin8(out_3[1]));
  _7408 u_7408_2 (
    .pin1(a[6]), .pin2(b[6]), .pin3(out_3[6]), .pin4(a[7]), .pin5(b[7]), .pin6(out_3[7]), .pin13(a[4]),
    .pin12(b[4]), .pin11(out_3[4]), .pin10(a[5]), .pin9(b[5]), .pin8(out_3[5]));
  _7408 u_7408_3 (
    .pin1(a[10]), .pin2(b[10]), .pin3(out_3[10]), .pin4(a[11]), .pin5(b[11]), .pin6(out_3[11]), .pin13(a[8]),
    .pin12(b[8]), .pin11(out_3[8]), .pin10(a[9]), .pin9(b[9]), .pin8(out_3[9]));
  _7408 u_7408_4 (
    .pin1(a[14]), .pin2(b[14]), .pin3(out_3[14]), .pin4(a[15]), .pin5(b[15]), .pin6(out_3[15]),
    .pin13(a[12]), .pin12(b[12]), .pin11(out_3[12]), .pin10(a[13]), .pin9(b[13]), .pin8(out_3[13]));
endmodule

module or_16 (
  input  [15:0] a,
  input  [15:0] b,
  output [15:0] out_3
);

  _7432 u_7432_1 (
    .pin1(a[2]), .pin2(b[2]), .pin3(out_3[2]), .pin4(a[3]), .pin5(b[3]), .pin6(out_3[3]), .pin13(a[0]),
    .pin12(b[0]), .pin11(out_3[0]), .pin10(a[1]), .pin9(b[1]), .pin8(out_3[1]));
  _7432 u_7432_2 (
    .pin1(a[6]), .pin2(b[6]), .pin3(out_3[6]), .pin4(a[7]), .pin5(b[7]), .pin6(out_3[7]), .pin13(a[4]),
    .pin12(b[4]), .pin11(out_3[4]), .pin10(a[5]), .pin9(b[5]), .pin8(out_3[5]));
  _7432 u_7432_3 (
    .pin1(a[10]), .pin2(b[10]), .pin3(out_3[10]), .pin4(a[11]), .pin5(b[11]), .pin6(out_3[11]), .pin13(a[8]),
    .pin12(b[8]), .pin11(out_3[8]), .pin10(a[9]), .pin9(b[9]), .pin8(out_3[9]));
  _7432 u_7432_4 (
    .pin1(a[14]), .pin2(b[14]), .pin3(out_3[14]), .pin4(a[15]), .pin5(b[15]), .pin6(out_3[15]),
    .pin13(a[12]), .pin12(b[12]), .pin11(out_3[12]), .pin10(a[13]), .pin9(b[13]), .pin8(out_3[13]));
endmodule

module xor_16 (
  input  [15:0] a,
  input  [15:0] b,
  output [15:0] out_3
);

  _7486 u_7486_1 (
    .pin1(a[2]), .pin2(b[2]), .pin3(out_3[2]), .pin4(a[3]), .pin5(b[3]), .pin6(out_3[3]), .pin13(a[0]),
    .pin12(b[0]), .pin11(out_3[0]), .pin10(a[1]), .pin9(b[1]), .pin8(out_3[1]));
  _7486 u_7486_2 (
    .pin1(a[6]), .pin2(b[6]), .pin3(out_3[6]), .pin4(a[7]), .pin5(b[7]), .pin6(out_3[7]), .pin13(a[4]),
    .pin12(b[4]), .pin11(out_3[4]), .pin10(a[5]), .pin9(b[5]), .pin8(out_3[5]));
  _7486 u_7486_3 (
    .pin1(a[10]), .pin2(b[10]), .pin3(out_3[10]), .pin4(a[11]), .pin5(b[11]), .pin6(out_3[11]), .pin13(a[8]),
    .pin12(b[8]), .pin11(out_3[8]), .pin10(a[9]), .pin9(b[9]), .pin8(out_3[9]));
  _7486 u_7486_4 (
    .pin1(a[14]), .pin2(b[14]), .pin3(out_3[14]), .pin4(a[15]), .pin5(b[15]), .pin6(out_3[15]),
    .pin13(a[12]), .pin12(b[12]), .pin11(out_3[12]), .pin10(a[13]), .pin9(b[13]), .pin8(out_3[13]));
endmodule

module flip_flop_8 (
  input  [7:0] data,
  input  clock,
  input  output_disable,
  output [7:0] o
);

  // DIP_74374 dip_74374_1: pin names not known; wires that end beside it: output_disable, o[7], o[0], data[7], data[0], data[6], data[1], o[6], o[1], o[5], o[2], data[5], data[2], data[4], data[3], o[4], o[3], clock
endmodule

module or_8 (
  input  [7:0] in_1,
  input  [7:0] in_2,
  output [7:0] out_3
);

  _7432 u_7432_1 (
    .pin1(in_1[2]), .pin2(in_2[2]), .pin3(out_3[2]), .pin4(in_1[3]), .pin5(in_2[3]), .pin6(out_3[3]),
    .pin13(in_1[0]), .pin12(in_2[0]), .pin11(out_3[0]), .pin10(in_1[1]), .pin9(in_2[1]), .pin8(out_3[1]));
  _7432 u_7432_2 (
    .pin1(in_1[6]), .pin2(in_2[6]), .pin3(out_3[6]), .pin4(in_1[7]), .pin5(in_2[7]), .pin6(out_3[7]),
    .pin13(in_1[4]), .pin12(in_2[4]), .pin11(out_3[4]), .pin10(in_1[5]), .pin9(in_2[5]), .pin8(out_3[5]));
endmodule

module not_16 (
  input  [15:0] in_1,
  output [15:0] out_2
);

  _7419 u_7419_1 (
    .pin1(in_1[5]), .pin2(out_2[5]), .pin3(in_1[4]), .pin4(out_2[4]), .pin5(in_1[3]), .pin6(out_2[3]),
    .pin13(in_1[0]), .pin12(out_2[0]), .pin11(in_1[1]), .pin10(out_2[1]), .pin9(in_1[2]), .pin8(out_2[2]));
  _7419 u_7419_2 (
    .pin1(in_1[11]), .pin2(out_2[11]), .pin3(in_1[10]), .pin4(out_2[10]), .pin5(in_1[9]), .pin6(out_2[9]),
    .pin13(in_1[6]), .pin12(out_2[6]), .pin11(in_1[7]), .pin10(out_2[7]), .pin9(in_1[8]), .pin8(out_2[8]));
  _7419 u_7419_3 (
    .pin5(in_1[15]), .pin6(out_2[15]), .pin13(in_1[12]), .pin12(out_2[12]), .pin11(in_1[13]),
    .pin10(out_2[13]), .pin9(in_1[14]), .pin8(out_2[14]));  // open: pin1, pin2, pin3, pin4
endmodule

module switched_decoder_3 (
  input  [2:0] in_1,
  input  output_disable,
  output [7:0] decoded
);

  // DIP_74138 dip_74138_1: pin names not known; wires that end beside it: in_1[0], in_1[1], in_1[2], output_disable, 1'b0, 1'b1, decoded[7], decoded[0], decoded[1], decoded[2], decoded[3], decoded[4], decoded[5], decoded[6]
endmodule

module switched_decoder_4 (
  input  [3:0] in_1,
  input  chip_disable,
  output [15:0] out_3
);

  // DIP_74138 dip_74138_1: pin names not known; wires that end beside it: in_1[0], in_1[1], in_1[2], in_1[3], chip_disable, out_3[0], out_3[1], out_3[2], out_3[3]
  // DIP_74138 dip_74138_2: pin names not known; wires that end beside it: 1'b1, out_3[7], in_1[0], in_1[1], in_1[2], chip_disable, chip_disable, in_1[3], out_3[15], out_3[4], out_3[5], out_3[6], out_3[8], out_3[9], out_3[10], out_3[11], out_3[12], out_3[13], out_3[14]
endmodule

module switched_decoder_5 (
  input  [4:0] in_1,
  input  chip_disable,
  output [31:0] out_3
);

  wire dip_74138_1_p7, dip_74138_1_p8, dip_74138_1_p9, dip_74138_1_p10;

  // DIP_74138 dip_74138_1: pin names not known; wires that end beside it: in_1[3], in_1[4], 1'b0, chip_disable, chip_disable, 1'b1, dip_74138_1_p7, dip_74138_1_p8, dip_74138_1_p9, dip_74138_1_p10
  // DIP_74138 dip_74138_2: pin names not known; wires that end beside it: in_1[0], in_1[1], in_1[2], dip_74138_1_p7, dip_74138_1_p7, out_3[0], out_3[1], out_3[2], out_3[3]
  // DIP_74138 dip_74138_3: pin names not known; wires that end beside it: 1'b1, out_3[7], in_1[0], in_1[1], in_1[2], dip_74138_1_p8, dip_74138_1_p8, out_3[4], out_3[5], out_3[6], out_3[8], out_3[9], out_3[10], out_3[11]
  // DIP_74138 dip_74138_4: pin names not known; wires that end beside it: 1'b1, out_3[15], in_1[0], in_1[1], in_1[2], dip_74138_1_p9, dip_74138_1_p9, out_3[12], out_3[13], out_3[14], out_3[16], out_3[17], out_3[18], out_3[19]
  // DIP_74138 dip_74138_5: pin names not known; wires that end beside it: 1'b1, out_3[23], in_1[0], in_1[1], in_1[2], dip_74138_1_p10, dip_74138_1_p10, 1'b1, out_3[31], out_3[20], out_3[21], out_3[22], out_3[24], out_3[25], out_3[26], out_3[27], out_3[28], out_3[29], out_3[30]
endmodule

module logical_comparator_16 (
  input  [15:0] A,
  input  [15:0] B,
  output A_lt_B,
  output A_eq_B,
  output A_gt_B
);

  wire n7485_1_pin2, n7485_1_pin3, n7485_1_pin5, n7485_1_pin6, n7485_1_pin7, n7485_2_pin3, n7485_2_pin5,
       n7485_2_pin6, n7485_2_pin7, n7485_3_pin3, n7485_3_pin5, n7485_3_pin6, n7485_3_pin7, n7485_4_pin1,
       n7485_4_pin5, n7485_4_pin6, n7485_4_pin7, n7485_5_pin1;

  _7485 #(.ShowInternalStructure("true")) u_7485_1 (
    .pin1(B[3]), .pin2(n7485_1_pin2), .pin3(n7485_1_pin3), .pin4(n7485_1_pin2), .pin5(n7485_1_pin5),
    .pin6(n7485_1_pin6), .pin7(n7485_1_pin7), .pin15(A[3]), .pin14(B[2]), .pin13(A[2]), .pin12(A[1]),
    .pin11(B[1]), .pin10(A[0]), .pin9(B[0]));
  _7485 #(.ShowInternalStructure("true")) u_7485_2 (
    .pin1(B[8]), .pin2(B[4]), .pin3(n7485_2_pin3), .pin4(A[4]), .pin5(n7485_2_pin5), .pin6(n7485_2_pin6),
    .pin7(n7485_2_pin7), .pin15(A[8]), .pin14(B[7]), .pin13(A[7]), .pin12(A[6]), .pin11(B[6]), .pin10(A[5]),
    .pin9(B[5]));
  _7485 #(.ShowInternalStructure("true")) u_7485_3 (
    .pin1(B[13]), .pin2(B[9]), .pin3(n7485_3_pin3), .pin4(A[9]), .pin5(n7485_3_pin5), .pin6(n7485_3_pin6),
    .pin7(n7485_3_pin7), .pin15(A[13]), .pin14(B[12]), .pin13(A[12]), .pin12(A[11]), .pin11(B[11]),
    .pin10(A[10]), .pin9(B[10]));
  _7485 #(.ShowInternalStructure("true")) u_7485_4 (
    .pin1(n7485_4_pin1), .pin2(B[14]), .pin3(n7485_4_pin1), .pin4(A[14]), .pin5(n7485_4_pin5),
    .pin6(n7485_4_pin6), .pin7(n7485_4_pin7), .pin15(n7485_4_pin1), .pin14(n7485_4_pin1),
    .pin13(n7485_4_pin1), .pin12(n7485_4_pin1), .pin11(n7485_4_pin1), .pin10(A[15]), .pin9(B[15]));
  // NoConnect on n7485_2_pin6
  // NoConnect on n7485_3_pin6
  // NoConnect on n7485_4_pin6
  _7485 #(.ShowInternalStructure("true")) u_7485_5 (
    .pin1(n7485_5_pin1), .pin2(n7485_1_pin7), .pin3(n7485_1_pin6), .pin4(n7485_1_pin5), .pin5(A_gt_B),
    .pin6(A_eq_B), .pin7(A_lt_B), .pin15(n7485_5_pin1), .pin14(n7485_4_pin7), .pin13(n7485_4_pin5),
    .pin12(n7485_3_pin5), .pin11(n7485_3_pin7), .pin10(n7485_2_pin5), .pin9(n7485_2_pin7));
  // also tied to GND on the sheet: {n7485_2_pin3, n7485_3_pin3, n7485_4_pin1, n7485_1_pin2, n7485_5_pin1}
  // also tied to VCC on the sheet: n7485_1_pin3
endmodule

module ps2_shift_reg (
  input  [7:0] write_value,
  input  clock,
  input  not_write,
  output serial_out,
  output [7:0] read_value
);

  wire n74165_1_pin10, n74165_1_pin15;

  _74165 #(.ShowInternalStructure("true")) u_74165_1 (
    .pin1(not_write), .pin2(clock), .pin3(write_value[4]), .pin4(write_value[5]), .pin5(write_value[6]),
    .pin6(write_value[7]), .pin15(n74165_1_pin15), .pin14(write_value[3]), .pin13(write_value[2]),
    .pin12(write_value[1]), .pin11(write_value[0]), .pin10(n74165_1_pin10), .pin9(serial_out));  // open: pin7
  // also tied to GND on the sheet: n74165_1_pin15
endmodule

module input_buffer_8 (
  input  in_1,
  input  in_2,
  input  in_3,
  input  in_4,
  input  in_5,
  input  in_6,
  input  in_7,
  input  in_8,
  input  not_clear,
  output out_10,
  output out_11,
  output out_12,
  output out_13,
  output out_14,
  output out_15,
  output out_16,
  output out_17
);

  wire n7404_1_pin2, n7404_1_pin4, n7404_1_pin6, n7404_1_pin8, n7404_1_pin10, n7404_1_pin12, n7404_2_pin10,
       n7404_2_pin12;

  _7404 u_7404_1 (
    .pin1(in_4), .pin2(n7404_1_pin2), .pin3(in_5), .pin4(n7404_1_pin4), .pin5(in_6), .pin6(n7404_1_pin6),
    .pin13(in_2), .pin12(n7404_1_pin12), .pin11(in_1), .pin10(n7404_1_pin10), .pin9(in_3), .pin8(n7404_1_pin8));
  _7404 u_7404_2 (
    .pin13(in_7), .pin12(n7404_2_pin12), .pin11(in_8), .pin10(n7404_2_pin10));  // open: pin1, pin2, pin3, pin4, pin5, pin6, pin9, pin8
  _7474 #(.ShowInternalStructure("true")) u_7474_1 (
    .pin1(not_clear), .pin4(n7404_1_pin12), .pin6(out_11), .pin13(not_clear), .pin10(n7404_1_pin10),
    .pin8(out_10));  // open: pin2, pin3, pin5, pin12, pin11, pin9
  _7474 #(.ShowInternalStructure("true")) u_7474_2 (
    .pin1(not_clear), .pin4(n7404_1_pin2), .pin6(out_13), .pin13(not_clear), .pin10(n7404_1_pin8),
    .pin8(out_12));  // open: pin2, pin3, pin5, pin12, pin11, pin9
  _7474 #(.ShowInternalStructure("true")) u_7474_3 (
    .pin1(not_clear), .pin4(n7404_1_pin6), .pin6(out_15), .pin13(not_clear), .pin10(n7404_1_pin4),
    .pin8(out_14));  // open: pin2, pin3, pin5, pin12, pin11, pin9
  _7474 #(.ShowInternalStructure("true")) u_7474_4 (
    .pin1(not_clear), .pin4(n7404_2_pin10), .pin6(out_17), .pin13(not_clear), .pin10(n7404_2_pin12),
    .pin8(out_16));  // open: pin2, pin3, pin5, pin12, pin11, pin9

  // Notes on the sheet:
  //   not_clear: initial=0x1
endmodule

module ps2_controller (
  input  ps2_din,
  input  ps2_clk,
  output not_output_ready,
  output [7:0] recieved_byte,
  output parity_failed
);

  wire n7404_1_pin6, n7486_1_pin1, n7486_1_pin3, n7486_1_pin6, n7486_1_pin12, n7486_2_pin2, n7486_2_pin4,
       n7486_2_pin5, n74125_1_pin1, n74125_1_pin4, n74125_1_pin6, n74161_1_pin1, n74161_1_pin7,
       n74164_1_pin2, n74164_1_pin3, n74164_1_pin8, n74164_2_pin11;

  _74164 #(.ShowInternalStructure("true")) u_74164_1 (
    .pin1(recieved_byte[7]), .pin2(n74164_1_pin2), .pin3(n74164_1_pin3), .pin4(recieved_byte[0]),
    .pin5(recieved_byte[1]), .pin6(recieved_byte[2]), .pin13(recieved_byte[6]), .pin12(recieved_byte[5]),
    .pin11(recieved_byte[4]), .pin10(recieved_byte[3]), .pin8(n74164_1_pin8));  // open: pin9
  _74125 #(.ShowInternalStructure("true")) u_74125_1 (
    .pin1(n74125_1_pin1), .pin2(ps2_clk), .pin3(n74164_1_pin8), .pin4(n74125_1_pin4), .pin5(ps2_clk),
    .pin6(n74125_1_pin6));  // open: pin13, pin12, pin11, pin10, pin9, pin8
  not not_1 (n74125_1_pin1, n74125_1_pin4);
  Pull_Resistor pull_resistor_1 (.node(n74164_1_pin8));
  _74161 #(.ShowInternalStructure("true")) u_74161_1 (
    .pin1(n74161_1_pin1), .pin2(ps2_clk), .pin7(n74161_1_pin7), .pin11(n74125_1_pin4), .pin10(n74161_1_pin7),
    .pin9(n74161_1_pin7));  // open: pin3, pin4, pin5, pin6, pin15, pin14, pin13, pin12
  Pull_Resistor pull_resistor_2 (.node(n74125_1_pin6));
  _74164 #(.ShowInternalStructure("true")) u_74164_2 (
    .pin1(ps2_din), .pin2(n74164_1_pin2), .pin12(recieved_byte[7]), .pin11(n74164_2_pin11),
    .pin8(n74125_1_pin6));  // open: pin3, pin4, pin5, pin6, pin13, pin10, pin9
  _7404 u_7404_1 (
    .pin5(recieved_byte[7]), .pin6(n7404_1_pin6));  // open: pin1, pin2, pin3, pin4, pin13, pin12, pin11, pin10, pin9, pin8
  _7432 #(.ShowInternalStructure("true")) u_7432_1 (
    .pin1(n7404_1_pin6), .pin2(n74164_1_pin3), .pin3(not_output_ready));  // open: pin4, pin5, pin6, pin13, pin12, pin11, pin10, pin9, pin8
  _7486 #(.ShowInternalStructure("true")) u_7486_1 (
    .pin1(n7486_1_pin1), .pin2(recieved_byte[7]), .pin3(n7486_1_pin3), .pin4(n7486_1_pin3),
    .pin5(recieved_byte[6]), .pin6(n7486_1_pin6), .pin13(recieved_byte[2]), .pin12(n7486_1_pin12),
    .pin11(n7486_1_pin1), .pin10(recieved_byte[1]), .pin9(recieved_byte[0]), .pin8(n7486_1_pin12));
  _7486 u_7486_2 (
    .pin1(n74164_2_pin11), .pin2(n7486_2_pin2), .pin3(parity_failed), .pin4(n7486_2_pin4),
    .pin5(n7486_2_pin5), .pin6(n7486_2_pin2), .pin13(recieved_byte[3]), .pin12(recieved_byte[4]),
    .pin11(n7486_2_pin4), .pin10(recieved_byte[5]), .pin9(n7486_1_pin6), .pin8(n7486_2_pin5));
  // also tied to VCC on the sheet: {n74164_1_pin2, n74161_1_pin7}
endmodule
